// Logisim project asdfasf.circ as structural Verilog
module datapath (
  input  clk,
  input  rst_n,
  input  [3:0] arr_size,
  input  [31:0] r_data,
  input  sl_1_incd_to_i,
  input  ld_i,
  input  clr_i,
  input  sl_i_minus_1_decrd_to_j,
  input  ld_j,
  input  clr_j,
  input  ld_elem2insert,
  input  clr_elem2insert,
  input  ld_elem2compare,
  input  clr_elem2compare,
  input  sl_i_j_to_arr_ra,
  input  sl_j_j_plus_1_to_arr_wa,
  input  sl_elem2insert_elem2compare_to_arr_w,
  output [3:0] ar_address,
  output [3:0] aw_address,
  output [31:0] w_data,
  output elem2insert_gt_elem2compare,
  output j_gte_0,
  output i_lt_arr_size
);
endmodule
