// Logisim project controller.circ as structural Verilog: 1 circuit, main circuit controller
module controller (
  input  start,
  input  ar_ready,
  input  r_valid,
  input  r_resp,
  input  aw_ready,
  input  w_ready,
  input  b_valid,
  input  b_resp,
  input  elem2insert_gt_elem2compare,
  input  j_gte_0,
  input  i_lt_arr_size,
  input  clk,
  input  rst_n,
  output done,
  output sl_1_incd_to_i,
  output ld_return_read_data,
  output error,
  output ld_i,
  output sl_j_j_plus_1_to_arg_write_addr,
  output ar_valid,
  output sl_elem2insert_elem2compare_to_arg_write_data,
  output sl_i_minus_1_decrd_to_j,
  output ld_arg_write_addr,
  output r_ready,
  output ld_arg_write_data,
  output ld_j,
  output aw_valid,
  output ld_elem2insert,
  output ld_elem2compare,
  output w_valid,
  output sl_i_j_to_arg_read_addr,
  output ld_arg_read_addr,
  output b_ready
);

  wire and_1_out, and_2_out, and_3_out, and_8_out, and_9_out, and_10_out, and_11_out, and_16_out, and_17_out,
       and_18_out, and_19_out, and_20_out, and_21_out, and_22_out, assign_i, assng_j, check_if_correct_place,
       complete_ar, complete_aw, complete_aw_and_w, complete_aw_wait_w_ready, complete_w,
       complete_w_wait_aw_ready, gen_assign_i, gen_complete_ar, gen_complete_aw, gen_complete_aw_and_w,
       gen_complete_aw_wait_w_ready, gen_complete_w, gen_complete_w_wait_aw_ready, gen_done, gen_err,
       gen_inc_i, gen_outer_loop_check, gen_process_b_resp, gen_process_r_data_resp, gen_read_arr_i,
       gen_read_arr_j, gen_read_function, gen_return_read_fn, gen_return_write_fn,
       gen_shift_elem2insert_left, ld_arg_return_state, reset, sl_to_state;
  wire [1:0] sl_to_arg_return_state;
  wire [5:0] arg_return_state_q, d_arg_return_state;
  wire [29:0] gen_state;
  wire [31:0] current_state, decoder_1_out0;
  wire [32:0] next_state;

  not not_1 (reset, rst_n);
  and and_1 (and_1_out, current_state[2], ~i_lt_arr_size);  // AND_Gate
  and and_2 (and_2_out, current_state[7], ~j_gte_0);  // AND_Gate
  and and_3 (and_3_out, check_if_correct_place, elem2insert_gt_elem2compare);
  or or_1 (ar_valid, current_state[15], current_state[16]);
  or or_2 (r_ready, complete_ar, current_state[18]);
  or or_3 (aw_valid, current_state[22], current_state[23], complete_w_wait_aw_ready);
  or or_4 (w_valid, current_state[22], current_state[23], complete_aw_wait_w_ready);
  or or_5 (b_ready, complete_aw, complete_w, complete_aw_and_w, current_state[29]);
  and and_4 (gen_state[0], current_state[0], ~start);  // AND_Gate
  and and_5 (gen_assign_i, current_state[0], start);
  or or_6 (gen_outer_loop_check, assign_i, sl_1_incd_to_i);
  or or_7 (gen_done, and_1_out, done);
  and and_6 (gen_read_arr_i, current_state[2], i_lt_arr_size);
  or or_8 (gen_inc_i, and_2_out, and_3_out, sl_i_minus_1_decrd_to_j);
  and and_7 (gen_read_arr_j, current_state[7], j_gte_0);
  Register #(.width(6)) arg_return_state (
    .D(d_arg_return_state), .en(ld_arg_return_state), .clk(clk), .Q(arg_return_state_q), .clr(reset));
  or or_9 (ld_i, sl_1_incd_to_i, assign_i);
  or or_10 (ld_j, sl_i_minus_1_decrd_to_j, assng_j);
  or or_11 (ld_arg_read_addr, current_state[4], sl_i_j_to_arg_read_addr);
  Decoder #(.enable("false"), .select(5)) decoder_1 (
    .out0(decoder_1_out0[0]), .out1(decoder_1_out0[1]), .out2(decoder_1_out0[2]), .out3(decoder_1_out0[3]),
    .out4(decoder_1_out0[4]), .out5(decoder_1_out0[5]), .out6(decoder_1_out0[6]), .out7(decoder_1_out0[7]),
    .out8(decoder_1_out0[8]), .out9(decoder_1_out0[9]), .out10(decoder_1_out0[10]),
    .out11(decoder_1_out0[11]), .out12(decoder_1_out0[12]), .out13(decoder_1_out0[13]),
    .out14(decoder_1_out0[14]), .out15(decoder_1_out0[15]), .out16(decoder_1_out0[16]),
    .out17(decoder_1_out0[17]), .out18(decoder_1_out0[18]), .out19(decoder_1_out0[19]),
    .out20(decoder_1_out0[20]), .out21(decoder_1_out0[21]), .out22(decoder_1_out0[22]),
    .out23(decoder_1_out0[23]), .out24(decoder_1_out0[24]), .out25(decoder_1_out0[25]),
    .out26(decoder_1_out0[26]), .out27(decoder_1_out0[27]), .out28(decoder_1_out0[28]),
    .out29(decoder_1_out0[29]), .out30(decoder_1_out0[30]), .out31(decoder_1_out0[31]),
    .sel(arg_return_state_q[4:0]));
  Multiplexer #(.width(33)) multiplexer_1 (
    .in0({gen_err, gen_return_write_fn, gen_process_b_resp, gen_state[29], gen_complete_aw_and_w, gen_complete_w, gen_complete_aw_wait_w_ready, gen_complete_aw, gen_complete_w_wait_aw_ready, gen_state[23], current_state[21], gen_state[21], gen_return_read_fn, gen_process_r_data_resp, gen_state[18], gen_complete_ar, gen_state[16], gen_read_function, 2'b00, gen_shift_elem2insert_left, ld_elem2compare, 1'b0, gen_read_arr_j, gen_inc_i, assng_j, ld_elem2insert, 1'b0, gen_read_arr_i, gen_done, gen_outer_loop_check, gen_assign_i, gen_state[0]}),
    .in1({arg_return_state_q[5], decoder_1_out0}), .out(next_state), .sel(sl_to_state));
  and and_8 (and_8_out, current_state[16], ~ar_ready);  // AND_Gate
  and and_9 (and_9_out, current_state[18], ~r_valid);  // AND_Gate
  and and_10 (and_10_out, current_state[23], ~aw_ready, ~w_ready);  // AND_Gate
  and and_11 (and_11_out, 1'b1, clk);
  Register #(.width(32)) register_1 (
    .D(next_state[32:1]), .en(1'b1), .clk(clk),
    .Q({error, current_state[31:29], complete_aw_and_w, complete_w, complete_aw_wait_w_ready, complete_aw, complete_w_wait_aw_ready, current_state[23:20], ld_return_read_data, current_state[18], complete_ar, current_state[16:15], sl_i_minus_1_decrd_to_j, sl_elem2insert_elem2compare_to_arg_write_data, current_state[12], check_if_correct_place, ld_elem2compare, sl_i_j_to_arg_read_addr, sl_1_incd_to_i, current_state[7], assng_j, ld_elem2insert, current_state[4], done, current_state[2], assign_i}),
    .clr(reset));
  and and_12 (gen_shift_elem2insert_left, check_if_correct_place, ~elem2insert_gt_elem2compare);  // AND_Gate
  or or_12 (gen_read_function, current_state[4], sl_i_j_to_arg_read_addr);
  or or_13 (gen_state[16], current_state[15], and_8_out);
  and and_13 (gen_complete_ar, current_state[16], ar_ready);
  or or_14 (gen_state[18], complete_ar, and_9_out);
  and and_14 (gen_process_r_data_resp, current_state[18], r_valid);
  and and_15 (gen_return_read_fn, ld_return_read_data, r_resp);
  or or_15 (gen_state[21], current_state[12], sl_elem2insert_elem2compare_to_arg_write_data);
  or or_16 (gen_state[23], current_state[22], and_10_out);
  D_Flip_Flop d_ff_1 (
    .D(next_state[0]), .clk(and_11_out), .Q(current_state[0]), .preset(reset), .reset(1'b0));  // open: Qn
  or or_17 (ld_arg_write_addr, sl_elem2insert_elem2compare_to_arg_write_data, current_state[12]);
  or or_18 (ld_arg_return_state, current_state[4], sl_i_j_to_arg_read_addr, current_state[12], sl_elem2insert_elem2compare_to_arg_write_data);
  or or_19 (sl_to_state, current_state[20], current_state[31]);
  Priority_Encoder #(.select(2)) priority_encoder_1 (
    .in0(current_state[4]), .in1(sl_i_j_to_arg_read_addr), .in2(current_state[12]),
    .in3(sl_elem2insert_elem2compare_to_arg_write_data), .out(sl_to_arg_return_state),
    .en_in(ld_arg_return_state));  // open: gs, en_out
  Multiplexer #(.select(2), .width(6)) multiplexer_2 (
    .in0(6'b000101), .in1(6'b001010), .in2(6'b001101), .in3(6'b001110), .out(d_arg_return_state),
    .sel(sl_to_arg_return_state));
  and and_16 (and_16_out, current_state[29], ~b_valid);  // AND_Gate
  and and_17 (and_17_out, current_state[23], w_ready, ~aw_ready);  // AND_Gate
  and and_18 (and_18_out, complete_w_wait_aw_ready, ~aw_ready);  // AND_Gate
  and and_19 (and_19_out, complete_aw_wait_w_ready, ~w_ready);  // AND_Gate
  and and_20 (and_20_out, ld_return_read_data, ~r_resp);  // AND_Gate
  and and_21 (and_21_out, current_state[30], ~b_resp);  // AND_Gate
  or or_20 (gen_complete_w_wait_aw_ready, and_17_out, and_18_out);
  or or_21 (gen_complete_aw_wait_w_ready, and_19_out, and_22_out);
  and and_22 (and_22_out, current_state[23], ~w_ready, aw_ready);  // AND_Gate
  and and_23 (gen_complete_aw, complete_w_wait_aw_ready, aw_ready);
  and and_24 (gen_complete_w, complete_aw_wait_w_ready, w_ready);
  and and_25 (gen_complete_aw_and_w, current_state[23], w_ready, aw_ready);
  and and_26 (gen_process_b_resp, current_state[29], b_valid);
  and and_27 (gen_return_write_fn, current_state[30], b_resp);
  or or_22 (gen_err, and_20_out, and_21_out);
  or or_23 (gen_state[29], complete_aw_and_w, complete_w, complete_aw, and_16_out);

  assign ld_arg_write_data = ld_arg_write_addr;
  assign sl_j_j_plus_1_to_arg_write_addr = sl_elem2insert_elem2compare_to_arg_write_data;

  // Other names for the same wires on the sheet: wait_start = current_state[0];
  //   current_state (some bits) = {error, complete_aw_and_w, complete_w, complete_aw_wait_w_ready, complete_aw, complete_w_wait_aw_ready, ld_return_read_data, complete_ar, sl_i_minus_1_decrd_to_j, sl_elem2insert_elem2compare_to_arg_write_data, check_if_correct_place, ld_elem2compare, sl_i_j_to_arg_read_addr, sl_1_incd_to_i, assng_j, ld_elem2insert, done, assign_i};
  //   outer_loop_check = current_state[2]; read_arr_i = current_state[4]; assign_elem2insert = ld_elem2insert;
  //   gen_assng_j = ld_elem2insert;
  //   gen_state (some bits) = {gen_err, gen_return_write_fn, gen_process_b_resp, gen_complete_aw_and_w, gen_complete_w, gen_complete_aw_wait_w_ready, gen_complete_aw, gen_complete_w_wait_aw_ready, current_state[21], gen_return_read_fn, gen_process_r_data_resp, gen_complete_ar, gen_read_function, gen_shift_elem2insert_left, ld_elem2compare, gen_read_arr_j, gen_inc_i, assng_j, ld_elem2insert, gen_read_arr_i, gen_done, gen_outer_loop_check, gen_assign_i};
  //   gen_inner_loop_check = assng_j; inner_loop_check = current_state[7]; inc_i = sl_1_incd_to_i;
  //   read_arr_j = sl_i_j_to_arg_read_addr; assign_elem2compare = ld_elem2compare;
  //   gen_check_if_correct_place = ld_elem2compare; shift_elem2insert_left = current_state[12];
  //   shif_elem2compare_right = sl_elem2insert_elem2compare_to_arg_write_data; decrmt_j_t = sl_i_minus_1_decrd_to_j;
  //   read_function = current_state[15]; wait_ar_ready = current_state[16]; wait_r_valid = current_state[18];
  //   process_r_data_resp = ld_return_read_data; return_read_fn = current_state[20];
  //   gen_send_addr_and_data = current_state[21]; write_function = current_state[21];
  //   send_addr_and_data = current_state[22]; wait_aw_ready_or_w_ready = current_state[23];
  //   wait_b_valid = current_state[29]; process_b_resp = current_state[30]; return_write_fn = current_state[31];
  //   err = error; e2ins_gt_e2cmp = elem2insert_gt_elem2compare; gen_wait_start = gen_state[0];
  //   gen_wait_ar_ready = gen_state[16]; gen_wait_r_valid = gen_state[18]; gen_write_function = gen_state[21];
  //   gen_wait_aw_ready_or_w_ready = gen_state[23]; gen_wait_b_valid = gen_state[29]

  // Notes on the sheet:
  //   Output Generation
  //   Next State Generation
  //   onehot encoding
  //   Internal Control Signal Generation
  //   those states reached via function return
endmodule
