// Logisim project datapath.circ as structural Verilog: 1 circuit, main circuit datapath
module datapath (
  input  [3:0] arr_size,
  input  ld_elem2compare,
  input  ld_j,
  input  sl_i_minus_1_decrd_to_j,
  input  ld_i,
  input  sl_1_incd_to_i,
  input  ld_elem2insert,
  input  ld_arg_write_data,
  input  sl_elem2insert_elem2compare_to_arg_write_data,
  input  ld_arg_read_addr,
  input  sl_i_j_to_arg_read_addr,
  input  ld_arg_write_addr,
  input  sl_j_j_plus_1_to_arg_write_addr,
  input  [31:0] r_data,
  input  ld_return_read_data,
  input  clk,
  input  rst_n,
  output elem2insert_gt_elem2compare,
  output j_gte_0,
  output i_lt_arr_size,
  output [31:0] w_data,
  output [3:0] ar_address,
  output [3:0] aw_address
);

  wire comparator_2_lt, not_1_out;
  wire [4:0] adder_1_out, adder_2_out, i_q, j_q, multiplexer_1_out, multiplexer_2_out, multiplexer_3_out,
       subtractor_1_out;
  wire [31:0] elem2compare_q, elem2insert_q, multiplexer_4_out, read_return_data_q;

  not not_1 (not_1_out, rst_n);
  Multiplexer #(.width(5)) multiplexer_1 (
    .in0(5'b00001), .in1(adder_1_out), .out(multiplexer_1_out), .sel(sl_1_incd_to_i));
  Adder #(.width(5)) adder_1 (.a(5'b00001), .b(i_q), .out(adder_1_out), .cin(1'b0));  // open: cout
  Register #(.width(5)) i (.D(multiplexer_1_out), .en(ld_i), .clk(clk), .Q(i_q), .clr(not_1_out));
  Register #(.width(4)) arg_read_addr (
    .D(multiplexer_3_out[3:0]), .en(ld_arg_read_addr), .clk(clk), .Q(ar_address), .clr(not_1_out));
  Register #(.width(32)) elem2insert (
    .D(read_return_data_q), .en(ld_elem2insert), .clk(clk), .Q(elem2insert_q), .clr(not_1_out));
  Register #(.width(32)) arg_write_data (
    .D(multiplexer_4_out), .en(ld_arg_write_data), .clk(clk), .Q(w_data), .clr(not_1_out));
  Multiplexer #(.width(5)) multiplexer_2 (.in0(i_q), .in1(j_q), .out(multiplexer_2_out), .sel(sl_i_minus_1_decrd_to_j));
  Adder #(.width(5)) adder_2 (
    .a(j_q), .b({5{1'b0}}), .out(adder_2_out), .cin(sl_j_j_plus_1_to_arg_write_addr));  // open: cout
  Register #(.width(5)) j (.D(subtractor_1_out), .en(ld_j), .clk(clk), .Q(j_q), .clr(not_1_out));
  Subtractor #(.width(5)) subtractor_1 (
    .a(multiplexer_2_out), .b(5'b00001), .out(subtractor_1_out), .bin(1'b0));  // open: bout
  Register #(.width(4)) arg_write_addr (
    .D(adder_2_out[3:0]), .en(ld_arg_write_addr), .clk(clk), .Q(aw_address), .clr(not_1_out));
  Multiplexer #(.width(5)) multiplexer_3 (.in0(i_q), .in1(j_q), .out(multiplexer_3_out), .sel(sl_i_j_to_arg_read_addr));
  Register #(.width(32)) elem2compare (
    .D(read_return_data_q), .en(ld_elem2compare), .clk(clk), .Q(elem2compare_q), .clr(not_1_out));
  Register #(.width(32)) read_return_data (
    .D(r_data), .en(ld_return_read_data), .clk(clk), .Q(read_return_data_q), .clr(not_1_out));
  Comparator #(.width(32)) comparator_1 (
    .a(elem2insert_q), .b(elem2compare_q), .gt(elem2insert_gt_elem2compare));  // open: eq, lt
  Multiplexer #(.width(32)) multiplexer_4 (
    .in0(elem2insert_q), .in1(elem2compare_q), .out(multiplexer_4_out),
    .sel(sl_elem2insert_elem2compare_to_arg_write_data));
  Comparator #(.width(5)) comparator_2 (.a(j_q), .b({5{1'b0}}), .lt(comparator_2_lt));  // open: gt, eq
  not not_2 (j_gte_0, comparator_2_lt);
  Comparator #(.width(5)) comparator_3 (.a({1'b0, arr_size}), .b(i_q), .gt(i_lt_arr_size));  // open: eq, lt

  // Notes on the sheet:
  //   rst
endmodule
