// Logisim project memory.circ as structural Verilog: 1 circuit, main circuit memory
module memory (
  input  clk,
  input  rst_n,
  input  ar_valid,
  input  [3:0] ar_address,
  input  aw_valid,
  input  [3:0] aw_address,
  input  [31:0] w_data,
  input  r_ready,
  input  w_valid,
  input  in_10,
  input  b_ready,
  input  in_12,
  output aw_ready,
  output ar_ready,
  output [31:0] r_data,
  output r_valid,
  output w_ready,
  output r_resp,
  output b_valid,
  output b_resp
);

  wire ld_data, ld_reg_addr, reset, sl_ram_w_to_data;
  wire [3:0] reg_addr, rnd;
  wire [31:0] multiplexer_1_out, ram_out;

  not not_1 (reset, rst_n);
  Random #(.width(4)) random_1 (.clr(reset), .next(1'b1), .clk(clk), .out(rnd));
  Register #(.width(4)) u_reg_addr (.D(ar_address), .en(ld_reg_addr), .clk(clk), .Q(reg_addr), .clr(reset));
  Multiplexer #(.width(32)) multiplexer_1 (
    .in0(ram_out), .in1(w_data), .out(multiplexer_1_out), .sel(sl_ram_w_to_data));
  Register #(.width(32)) reg_data (.D(multiplexer_1_out), .en(ld_data), .clk(clk), .Q(r_data), .clr(reset));
  RAM #(.addrWidth(4), .dataWidth(32)) ram_1 (
    .addr(reg_addr), .we(in_10), .oe(in_12), .clk(clk), .din(r_data), .dout(ram_out));

  // Other names for the same wires on the sheet: in_enable = in_10; out_enable = in_12; ram_in[31:0] = r_data;
  //   reg_data[31:0] = r_data
endmodule
