// Logisim project memory_module.circ as structural Verilog: 1 circuit, main circuit memory
module memory (
  input  ar_valid,
  input  aw_valid,
  input  [3:0] ar_address,
  input  [3:0] aw_address,
  input  [31:0] w_data,
  input  w_valid,
  input  r_ready,
  input  b_ready,
  input  clk,
  input  rst_n,
  input  always_success,
  input  always_error,
  output aw_ready,
  output ar_ready,
  output [31:0] r_data,
  output w_ready,
  output r_valid,
  output r_resp,
  output b_valid,
  output b_resp
);

  wire and_1_out, and_3_out, and_4_out, and_5_out, and_6_out, and_7_out, and_8_out, and_9_out, and_10_out,
       and_11_out, and_13_out, and_14_out, and_15_out, and_16_out, and_17_out, complete_ar, complete_aw,
       complete_b, complete_r, complete_w, gen_ar_transfer, gen_aw_transfer, gen_complete_b, gen_complete_r,
       gen_decide_random, gen_idle, ld_data, ld_reg_addr, nand_1_out, or_9_out, reset, sl_ram_w_to_data;
  wire [3:0] multiplexer_1_out, reg_addr, rnd;
  wire [14:6] gen_state;
  wire [17:0] current_state;
  wire [31:0] multiplexer_2_out, ram_out_t;

  and and_1 (and_1_out, current_state[0], ~ar_valid, ~aw_valid);  // AND_Gate
  or or_1 (gen_idle, and_1_out, complete_r, complete_b);
  and and_2 (gen_decide_random, current_state[0], ar_valid, aw_valid);
  and and_3 (and_3_out, current_state[0], ar_valid, ~aw_valid);  // AND_Gate
  or or_2 (gen_ar_transfer, and_3_out, and_4_out);
  and and_4 (and_4_out, current_state[1], ~rnd[0]);  // AND_Gate
  and and_5 (and_5_out, current_state[0], ~ar_valid, aw_valid);  // AND_Gate
  and and_6 (and_6_out, current_state[1], rnd[0]);
  not not_1 (reset, rst_n);
  or or_3 (gen_aw_transfer, and_5_out, and_6_out);
  and and_7 (and_7_out, current_state[6], ~r_ready);  // AND_Gate
  and and_8 (and_8_out, current_state[7], ~r_ready);  // AND_Gate
  and and_9 (and_9_out, current_state[6], r_ready);
  and and_10 (and_10_out, current_state[7], r_ready);
  and and_11 (and_11_out, current_state[10], ~w_valid);  // AND_Gate
  Multiplexer #(.width(4)) multiplexer_1 (.in0(ar_address), .in1(aw_address), .out(multiplexer_1_out), .sel(aw_ready));
  or or_4 (gen_state[6], and_7_out, and_8_out);
  or or_5 (gen_complete_r, and_9_out, and_10_out);
  or or_6 (gen_state[10], and_11_out, complete_aw);
  and and_12 (gen_state[11], current_state[10], w_valid);
  D_Flip_Flop d_ff_1 (.D(gen_idle), .clk(and_13_out), .Q(current_state[0]), .preset(reset), .reset(1'b0));  // open: Qn
  and and_13 (and_13_out, 1'b1, clk);
  Register #(.width(17)) register_1 (
    .D({complete_ar, gen_complete_b, current_state[13], gen_state[14], complete_w, w_ready, gen_state[11:10], aw_ready, gen_complete_r, current_state[5], gen_state[6], current_state[17], ar_ready, gen_aw_transfer, gen_ar_transfer, gen_decide_random}),
    .en(1'b1), .clk(clk),
    .Q({current_state[17], complete_b, current_state[15:13], complete_w, w_ready, current_state[10], complete_aw, complete_r, current_state[7:5], complete_ar, aw_ready, ar_ready, current_state[1]}),
    .clr(reset));
  Multiplexer #(.width(32)) multiplexer_2 (
    .in0(ram_out_t), .in1(w_data), .out(multiplexer_2_out), .sel(sl_ram_w_to_data));
  Register #(.width(4)) u_reg_addr (.D(multiplexer_1_out), .en(ld_reg_addr), .clk(clk), .Q(reg_addr), .clr(reset));
  Random #(.width(4)) random_1 (.clr(reset), .next(1'b1), .clk(clk), .out(rnd));
  Register #(.width(32)) reg_data (.D(multiplexer_2_out), .en(ld_data), .clk(clk), .Q(r_data), .clr(reset));
  and and_14 (and_14_out, current_state[15], ~b_ready);  // AND_Gate
  and and_15 (and_15_out, current_state[14], ~b_ready);  // AND_Gate
  and and_16 (and_16_out, current_state[14], b_ready);
  and and_17 (and_17_out, current_state[15], b_ready);
  or or_7 (gen_state[14], and_14_out, and_15_out);
  or or_8 (gen_complete_b, and_16_out, and_17_out);
  RAM #(.addrWidth(4), .asyncread("true"), .dataWidth(32)) ram_1 (
    .addr(reg_addr), .we(current_state[13]), .oe(current_state[17]), .clk(clk), .din(r_data), .dout(ram_out_t));
  nand nand_1 (nand_1_out, rnd[0], rnd[1], rnd[2], rnd[3]);
  or or_9 (or_9_out, nand_1_out, always_success);
  and and_18 (b_resp, or_9_out, ~always_error);  // AND_Gate
  or or_10 (b_valid, current_state[15], current_state[14]);
  or or_11 (r_valid, current_state[7], current_state[6]);
  not not_2 (sl_ram_w_to_data, current_state[5]);
  or or_12 (ld_data, current_state[5], w_ready);
  or or_13 (ld_reg_addr, aw_ready, ar_ready);

  assign r_resp = b_resp;

  // Other names for the same wires on the sheet: idle = current_state[0]; decide_random = current_state[1];
  //   wait_r_ready = current_state[6]; output_read_data = current_state[7];
  //   current_state (some bits) = {complete_b, complete_w, w_ready, complete_aw, complete_r, complete_ar, aw_ready, ar_ready};
  //   wait_w_valid = current_state[10]; wait_b_ready = current_state[14]; respond_b = current_state[15];
  //   gen_state (some bits) = {complete_ar, gen_complete_b, current_state[13], complete_w, w_ready, aw_ready, gen_complete_r, current_state[5], current_state[17], ar_ready, gen_aw_transfer, gen_ar_transfer, gen_decide_random, gen_idle};
  //   ar_transfer = ar_ready; gen_complete_ar = ar_ready; gen_register_read_data = current_state[17];
  //   out_enable = current_state[17]; RAM_out = current_state[17]; gen_wait_r_ready = gen_state[6];
  //   gen_output_read_data = current_state[5]; register_read_data = current_state[5]; aw_transfer = aw_ready;
  //   gen_complete_aw = aw_ready; sl_aw_address_to_addr = aw_ready; gen_wait_w_valid = gen_state[10];
  //   gen_w_transfer = gen_state[11]; gen_complete_w = w_ready; w_transfer = w_ready; gen_store_reg_data = complete_w;
  //   gen_wait_b_ready = gen_state[14]; gen_respond_b = current_state[13]; in_enable = current_state[13];
  //   store_reg_data = current_state[13]; gen_RAM_out = complete_ar; ram_in[31:0] = r_data; reg_data[31:0] = r_data

  // Notes on the sheet:
  //   AXI-Lite interface
  //   State Transition Logic
  //   Onehot Encoded State
  //   Other Components
  //   State Output Logic
endmodule
