// Logisim project sort_circuit.circ as structural Verilog: 5 circuits, main circuit main
module sort_circuit (
  input  start,
  input  [4:0] arr_size,
  input  ar_ready,
  input  r_valid,
  input  r_resp,
  input  [31:0] r_data,
  input  aw_ready,
  input  w_ready,
  input  b_valid,
  input  b_resp,
  input  clk,
  input  rst_n,
  output done,
  output err,
  output [3:0] ar_address,
  output ar_valid,
  output r_ready,
  output aw_valid,
  output [3:0] aw_address,
  output [31:0] w_data,
  output w_valid,
  output b_ready
);

  wire controller_1_ld_arg_read_addr, controller_1_ld_elem2compare, controller_1_ld_elem2insert,
       controller_1_ld_i, controller_1_ld_j, controller_1_ld_return_read_data, controller_1_sl_decrd_to_j,
       controller_1_sl_elem2compare_to_write_data, controller_1_sl_incd_to_i,
       controller_1_sl_j_plus_1_to_write_addr, controller_1_sl_j_to_arg_read_addr,
       controller_1_write_submodule_start, e2ins_gt_e2cmp, i_lt_arr_size, j_gte_0, write_submodule_b_resp,
       write_submodule_done;
  wire [3:0] datapath_1_write_addr;
  wire [31:0] datapath_1_write_data;

  controller controller_1 (
    .start(start), .ar_ready(ar_ready), .r_valid(r_valid), .r_resp(r_resp),
    .write_submodule_done(write_submodule_done), .write_submodule_b_resp(write_submodule_b_resp),
    .elem2insert_gt_elem2compare(e2ins_gt_e2cmp), .j_gte_0(j_gte_0), .i_lt_arr_size(i_lt_arr_size),
    .clk(clk), .rst_n(rst_n), .done(done), .sl_incd_to_i(controller_1_sl_incd_to_i),
    .ld_return_read_data(controller_1_ld_return_read_data), .error(err), .ld_i(controller_1_ld_i),
    .sl_j_plus_1_to_write_addr(controller_1_sl_j_plus_1_to_write_addr),
    .sl_elem2compare_to_write_data(controller_1_sl_elem2compare_to_write_data), .ar_valid(ar_valid),
    .sl_decrd_to_j(controller_1_sl_decrd_to_j), .write_submodule_start(controller_1_write_submodule_start),
    .r_ready(r_ready), .ld_j(controller_1_ld_j), .ld_elem2insert(controller_1_ld_elem2insert),
    .ld_elem2compare(controller_1_ld_elem2compare),
    .sl_j_to_arg_read_addr(controller_1_sl_j_to_arg_read_addr),
    .ld_arg_read_addr(controller_1_ld_arg_read_addr));
  datapath datapath_1 (
    .arr_size(arr_size), .ld_elem2insert(controller_1_ld_elem2insert),
    .ld_elem2compare(controller_1_ld_elem2compare), .ld_j(controller_1_ld_j),
    .sl_decrd_to_j(controller_1_sl_decrd_to_j), .ld_i(controller_1_ld_i),
    .sl_incd_to_i(controller_1_sl_incd_to_i),
    .sl_elem2compare_to_write_data(controller_1_sl_elem2compare_to_write_data),
    .sl_j_to_arg_read_addr(controller_1_sl_j_to_arg_read_addr),
    .ld_arg_read_addr(controller_1_ld_arg_read_addr),
    .sl_j_plus_1_to_write_addr(controller_1_sl_j_plus_1_to_write_addr), .r_data(r_data),
    .ld_return_read_data(controller_1_ld_return_read_data), .clk(clk), .rst_n(rst_n),
    .elem2insert_gt_elem2compare(e2ins_gt_e2cmp), .write_data(datapath_1_write_data), .j_gte_0(j_gte_0),
    .i_lt_arr_size(i_lt_arr_size), .ar_address(ar_address), .write_addr(datapath_1_write_addr));
  write_submodule write_submodule_1 (
    .start(controller_1_write_submodule_start), .aw_ready(aw_ready), .data(datapath_1_write_data),
    .addr(datapath_1_write_addr), .w_ready(w_ready), .b_valid(b_valid), .b_resp(b_resp), .clk(clk),
    .rst_n(rst_n), .aw_valid(aw_valid), .aw_address(aw_address), .done(write_submodule_done),
    .w_data(w_data), .resp(write_submodule_b_resp), .w_valid(w_valid), .b_ready(b_ready));
endmodule

module write_submodule (
  input  start,
  input  aw_ready,
  input  [31:0] data,
  input  [3:0] addr,
  input  w_ready,
  input  b_valid,
  input  b_resp,
  input  clk,
  input  rst_n,
  output aw_valid,
  output [3:0] aw_address,
  output done,
  output [31:0] w_data,
  output resp,
  output w_valid,
  output b_ready
);

  wire and_1_out, and_2_out, and_3_out, and_4_out, and_5_out, and_6_out, and_8_out, and_12_out, complete_aw,
       complete_aw_and_w, complete_aw_wait_w_ready, complete_w, complete_w_wait_aw_ready, gen_complete_aw,
       gen_complete_aw_and_w, gen_complete_aw_wait_w_ready, gen_complete_w, gen_complete_w_wait_aw_ready,
       gen_idle, gen_process_b_resp, gen_send_addr_and_data, reset;
  wire [4:1] gen_state;
  wire [6:1] curr_state;

  and and_1 (and_1_out, done, ~start);  // AND_Gate
  not not_1 (reset, rst_n);
  and and_2 (and_2_out, curr_state[1], ~aw_ready, ~w_ready);  // AND_Gate
  and and_3 (and_3_out, complete_w_wait_aw_ready, ~aw_ready);  // AND_Gate
  and and_4 (and_4_out, curr_state[1], ~aw_ready, w_ready);  // AND_Gate
  and and_5 (and_5_out, complete_aw_wait_w_ready, ~w_ready);  // AND_Gate
  and and_6 (and_6_out, curr_state[1], aw_ready, ~w_ready);  // AND_Gate
  or or_1 (gen_idle, and_1_out, curr_state[6]);
  and and_7 (gen_send_addr_and_data, done, start);
  or or_2 (gen_state[1], curr_state[3], and_2_out);
  or or_3 (gen_complete_w_wait_aw_ready, and_3_out, and_4_out);
  or or_4 (gen_complete_aw_wait_w_ready, and_5_out, and_6_out);
  Register #(.width(32)) reg_data (.D(data), .en(done), .clk(clk), .Q(w_data), .clr(reset));
  Register #(.width(1)) reg_b_resp (.D(b_resp), .en(1'b1), .clk(clk), .Q(resp), .clr(reset));
  D_Flip_Flop d_ff_1 (.D(gen_idle), .clk(and_8_out), .Q(done), .preset(reset), .reset(1'b0));  // open: Qn
  and and_8 (and_8_out, 1'b1, clk);
  Register #(.width(9)) register_1 (
    .D({gen_complete_aw_wait_w_ready, gen_complete_aw_and_w, gen_complete_w, gen_process_b_resp, gen_complete_aw, gen_state[4], gen_send_addr_and_data, gen_complete_w_wait_aw_ready, gen_state[1]}),
    .en(1'b1), .clk(clk),
    .Q({complete_aw_wait_w_ready, complete_aw_and_w, complete_w, curr_state[6], complete_aw, curr_state[4:3], complete_w_wait_aw_ready, curr_state[1]}),
    .clr(reset));
  Register #(.width(4)) reg_addr (.D(addr), .en(done), .clk(clk), .Q(aw_address), .clr(reset));
  and and_9 (gen_complete_w, complete_aw_wait_w_ready, w_ready);
  and and_10 (gen_complete_aw, complete_w_wait_aw_ready, aw_ready);
  and and_11 (gen_complete_aw_and_w, curr_state[1], aw_ready, w_ready);
  and and_12 (and_12_out, curr_state[4], ~b_valid);  // AND_Gate
  or or_5 (gen_state[4], and_12_out, complete_w, complete_aw, complete_aw_and_w);
  and and_13 (gen_process_b_resp, curr_state[4], b_valid);
  or or_6 (aw_valid, curr_state[3], curr_state[1], complete_w_wait_aw_ready);
  or or_7 (w_valid, curr_state[3], curr_state[1], complete_aw_wait_w_ready);
  or or_8 (b_ready, complete_aw, complete_w, curr_state[4], complete_aw_and_w);

  // Other names for the same wires on the sheet: curr_state (some bits) = {complete_aw_wait_w_ready, complete_aw_and_w, complete_w, complete_aw, complete_w_wait_aw_ready, done};
  //   idle = done; ld_reg_addr = done; ld_reg_data = done; wait_aw_ready_or_w_ready = curr_state[1];
  //   send_addr_and_data = curr_state[3]; wait_b_valid = curr_state[4]; process_b_resp = curr_state[6];
  //   gen_state (some bits) = {gen_complete_aw_wait_w_ready, gen_complete_aw_and_w, gen_complete_w, gen_process_b_resp, gen_complete_aw, gen_send_addr_and_data, gen_complete_w_wait_aw_ready, gen_idle};
  //   gen_wait_aw_ready_or_w_ready = gen_state[1]; gen_wait_b_valid = gen_state[4]; reg_addr[3:0] = aw_address;
  //   reg_b_resp = resp; reg_data[31:0] = w_data

  // Notes on the sheet:
  //   AXI-Lite interface
  //   Supermodule Interface
  //   State Generation
  //   Other Components
  //   Onehot Encoded State
  //   Output/Internal Control Signal Generation
endmodule

module controller (
  input  start,
  input  ar_ready,
  input  r_valid,
  input  r_resp,
  input  write_submodule_done,
  input  write_submodule_b_resp,
  input  elem2insert_gt_elem2compare,
  input  j_gte_0,
  input  i_lt_arr_size,
  input  clk,
  input  rst_n,
  output done,
  output sl_incd_to_i,
  output ld_return_read_data,
  output error,
  output ld_i,
  output sl_j_plus_1_to_write_addr,
  output sl_elem2compare_to_write_data,
  output ar_valid,
  output sl_decrd_to_j,
  output write_submodule_start,
  output r_ready,
  output ld_j,
  output ld_elem2insert,
  output ld_elem2compare,
  output sl_j_to_arg_read_addr,
  output ld_arg_read_addr
);

  wire and_1_out, and_2_out, and_3_out, and_9_out, and_11_out, and_13_out, and_14_out, and_15_out,
       and_16_out, and_17_out, assign_i, assng_j, check_if_correct_place, complete_ar, gen_assign_i,
       gen_complete_ar, gen_decrmt_j, gen_done, gen_err, gen_inc_i, gen_inner_loop_check,
       gen_outer_loop_check, gen_process_r_data_resp, gen_read_arr_i, gen_read_arr_j, gen_read_function,
       gen_return_read_fn, gen_shif_elem2compare_right, gen_shift_elem2insert_left, ld_arg_return_state,
       not_1_out, sl_to_arg_return_state;
  wire [4:0] arg_return_state_q, d_arg_return_state;
  wire [20:0] gen_state;
  wire [22:0] current_state;
  wire [23:0] decoder_1_out0, next_state;

  not not_1 (not_1_out, rst_n);
  and and_1 (and_1_out, current_state[2], ~i_lt_arr_size);  // AND_Gate
  and and_2 (and_2_out, current_state[7], ~j_gte_0);  // AND_Gate
  and and_3 (and_3_out, check_if_correct_place, elem2insert_gt_elem2compare);
  or or_1 (ar_valid, current_state[17], current_state[18]);
  or or_2 (r_ready, complete_ar, current_state[20]);
  and and_4 (gen_state[0], current_state[0], ~start);  // AND_Gate
  and and_5 (gen_assign_i, current_state[0], start);
  or or_3 (gen_outer_loop_check, assign_i, sl_incd_to_i);
  or or_4 (gen_done, and_1_out, done);
  and and_6 (gen_read_arr_i, current_state[2], i_lt_arr_size);
  or or_5 (gen_inner_loop_check, assng_j, sl_decrd_to_j);
  or or_6 (gen_inc_i, and_2_out, and_3_out);
  and and_7 (gen_read_arr_j, current_state[7], j_gte_0);
  Register #(.width(5)) arg_return_state (
    .D(d_arg_return_state), .en(ld_arg_return_state), .clk(clk), .Q(arg_return_state_q), .clr(not_1_out));
  or or_7 (ld_i, sl_incd_to_i, assign_i);
  or or_8 (ld_j, sl_decrd_to_j, assng_j);
  or or_9 (ld_arg_read_addr, current_state[4], sl_j_to_arg_read_addr);
  Decoder #(.enable("false"), .select(5)) decoder_1 (
    .out0(decoder_1_out0[0]), .out1(decoder_1_out0[1]), .out2(decoder_1_out0[2]), .out3(decoder_1_out0[3]),
    .out4(decoder_1_out0[4]), .out5(decoder_1_out0[5]), .out6(decoder_1_out0[6]), .out7(decoder_1_out0[7]),
    .out8(decoder_1_out0[8]), .out9(decoder_1_out0[9]), .out10(decoder_1_out0[10]),
    .out11(decoder_1_out0[11]), .out12(decoder_1_out0[12]), .out13(decoder_1_out0[13]),
    .out14(decoder_1_out0[14]), .out15(decoder_1_out0[15]), .out16(decoder_1_out0[16]),
    .out17(decoder_1_out0[17]), .out18(decoder_1_out0[18]), .out19(decoder_1_out0[19]),
    .out20(decoder_1_out0[20]), .out21(decoder_1_out0[21]), .out22(decoder_1_out0[22]),
    .out23(decoder_1_out0[23]), .sel(arg_return_state_q));  // open: out24, out25, out26, out27, out28, out29, out30, out31
  Multiplexer #(.width(24)) multiplexer_1 (
    .in0({gen_err, gen_return_read_fn, gen_process_r_data_resp, gen_state[20], gen_complete_ar, gen_state[18], gen_read_function, gen_decrmt_j, gen_state[15], gen_shif_elem2compare_right, gen_state[13], gen_shift_elem2insert_left, ld_elem2compare, 1'b0, gen_read_arr_j, gen_inc_i, gen_inner_loop_check, ld_elem2insert, 1'b0, gen_read_arr_i, gen_done, gen_outer_loop_check, gen_assign_i, gen_state[0]}),
    .in1(decoder_1_out0), .out(next_state), .sel(current_state[22]));
  Register #(.width(23)) register_1 (
    .D(next_state[23:1]), .en(1'b1), .clk(clk),
    .Q({error, current_state[22], ld_return_read_data, current_state[20], complete_ar, current_state[18:17], sl_decrd_to_j, current_state[15], sl_elem2compare_to_write_data, current_state[13:12], check_if_correct_place, ld_elem2compare, sl_j_to_arg_read_addr, sl_incd_to_i, current_state[7], assng_j, ld_elem2insert, current_state[4], done, current_state[2], assign_i}),
    .clr(not_1_out));
  and and_8 (gen_shift_elem2insert_left, check_if_correct_place, ~elem2insert_gt_elem2compare);  // AND_Gate
  or or_10 (gen_state[13], current_state[12], and_9_out);
  and and_9 (and_9_out, current_state[13], ~write_submodule_done);  // AND_Gate
  and and_10 (gen_shif_elem2compare_right, current_state[13], write_submodule_done);
  and and_11 (and_11_out, current_state[15], ~write_submodule_done);  // AND_Gate
  or or_11 (gen_state[15], and_11_out, sl_elem2compare_to_write_data);
  and and_12 (gen_decrmt_j, current_state[15], write_submodule_done);
  D_Flip_Flop d_ff_1 (
    .D(next_state[0]), .clk(clk), .Q(current_state[0]), .preset(not_1_out), .reset(1'b0));  // open: Qn
  or or_12 (write_submodule_start, current_state[12], sl_elem2compare_to_write_data);
  Multiplexer #(.width(5)) multiplexer_2 (
    .in0(5'b00101), .in1(5'b01010), .out(d_arg_return_state), .sel(sl_to_arg_return_state));
  and and_13 (and_13_out, current_state[18], ~ar_ready);  // AND_Gate
  and and_14 (and_14_out, current_state[20], ~r_valid);  // AND_Gate
  and and_15 (and_15_out, gen_shif_elem2compare_right, ~write_submodule_b_resp);  // AND_Gate
  and and_16 (and_16_out, ld_return_read_data, ~r_resp);  // AND_Gate
  and and_17 (and_17_out, gen_decrmt_j, ~write_submodule_b_resp);  // AND_Gate
  or or_13 (ld_arg_return_state, current_state[4], sl_j_to_arg_read_addr);
  or or_14 (gen_read_function, current_state[4], sl_j_to_arg_read_addr);
  or or_15 (gen_state[18], current_state[17], and_13_out);
  and and_18 (gen_complete_ar, current_state[18], ar_ready);
  or or_16 (gen_state[20], complete_ar, and_14_out);
  and and_19 (gen_process_r_data_resp, current_state[20], r_valid);
  and and_20 (gen_return_read_fn, ld_return_read_data, r_resp);
  or or_17 (gen_err, and_16_out, and_15_out, error, and_17_out);
  Priority_Encoder #(.select(1)) priority_encoder_1 (
    .in0(current_state[4]), .in1(sl_j_to_arg_read_addr), .out(sl_to_arg_return_state),
    .en_in(ld_arg_return_state));  // open: gs, en_out

  assign sl_j_plus_1_to_write_addr = sl_elem2compare_to_write_data;

  // Other names for the same wires on the sheet: wait_start = current_state[0];
  //   current_state (some bits) = {error, ld_return_read_data, complete_ar, sl_decrd_to_j, sl_elem2compare_to_write_data, check_if_correct_place, ld_elem2compare, sl_j_to_arg_read_addr, sl_incd_to_i, assng_j, ld_elem2insert, done, assign_i};
  //   outer_loop_check = current_state[2]; read_arr_i = current_state[4]; assign_elem2insert = ld_elem2insert;
  //   gen_assng_j = ld_elem2insert;
  //   gen_state (some bits) = {gen_err, gen_return_read_fn, gen_process_r_data_resp, gen_complete_ar, gen_read_function, gen_decrmt_j, gen_shif_elem2compare_right, gen_shift_elem2insert_left, ld_elem2compare, gen_read_arr_j, gen_inc_i, gen_inner_loop_check, ld_elem2insert, gen_read_arr_i, gen_done, gen_outer_loop_check, gen_assign_i};
  //   inner_loop_check = current_state[7]; inc_i = sl_incd_to_i; read_arr_j = sl_j_to_arg_read_addr;
  //   assign_elem2compare = ld_elem2compare; gen_check_if_correct_place = ld_elem2compare;
  //   shift_elem2insert_left = current_state[12]; wait_submodule_return1 = current_state[13];
  //   shif_elem2compare_right = sl_elem2compare_to_write_data; wait_submodule_return2 = current_state[15];
  //   decrmt_j = sl_decrd_to_j; read_function = current_state[17]; wait_ar_ready = current_state[18];
  //   wait_r_valid = current_state[20]; process_r_data_resp = ld_return_read_data; return_read_fn = current_state[22];
  //   sl_to_state = current_state[22]; err = error; e2ins_gt_e2cmp = elem2insert_gt_elem2compare;
  //   gen_wait_start = gen_state[0]; gen_wait_submodule_return1 = gen_state[13];
  //   gen_wait_submodule_return2 = gen_state[15]; gen_wait_ar_ready = gen_state[18]; gen_wait_r_valid = gen_state[20]

  // Notes on the sheet:
  //   Output Generation
  //   Next State Generation
  //   onehot encoding
  //   Internal Control Signal Generation
  //   those states reached via function return
endmodule

module datapath (
  input  [4:0] arr_size,
  input  ld_elem2insert,
  input  ld_elem2compare,
  input  ld_j,
  input  sl_decrd_to_j,
  input  ld_i,
  input  sl_incd_to_i,
  input  sl_elem2compare_to_write_data,
  input  sl_j_to_arg_read_addr,
  input  ld_arg_read_addr,
  input  sl_j_plus_1_to_write_addr,
  input  [31:0] r_data,
  input  ld_return_read_data,
  input  clk,
  input  rst_n,
  output elem2insert_gt_elem2compare,
  output [31:0] write_data,
  output j_gte_0,
  output i_lt_arr_size,
  output [3:0] ar_address,
  output [3:0] write_addr
);

  wire comparator_2_lt, reset;
  wire [4:0] adder_1_out, i, j, multiplexer_1_out, multiplexer_2_out, multiplexer_3_out, subtractor_1_out;
  wire [4:4] adder_2_out;
  wire [31:0] elem2compare_q, elem2ins, q_read_return_data;

  not not_1 (reset, rst_n);
  Multiplexer #(.width(5)) multiplexer_1 (
    .in0(5'b00001), .in1(adder_1_out), .out(multiplexer_1_out), .sel(sl_incd_to_i));
  Adder #(.width(5)) adder_1 (.a(5'b00001), .b(i), .out(adder_1_out), .cin(1'b0));  // open: cout
  Multiplexer #(.width(5)) multiplexer_2 (.in0(i), .in1(j), .out(multiplexer_2_out), .sel(sl_j_to_arg_read_addr));
  Register #(.width(5)) u_i (.D(multiplexer_1_out), .en(ld_i), .clk(clk), .Q(i), .clr(reset));
  Register #(.width(4)) arg_read_addr (
    .D(multiplexer_2_out[3:0]), .en(ld_arg_read_addr), .clk(clk), .Q(ar_address), .clr(reset));
  Register #(.width(32)) elem2insert (
    .D(q_read_return_data), .en(ld_elem2insert), .clk(clk), .Q(elem2ins), .clr(reset));
  Multiplexer #(.width(5)) multiplexer_3 (.in0(i), .in1(j), .out(multiplexer_3_out), .sel(sl_decrd_to_j));
  Register #(.width(5)) u_j (.D(subtractor_1_out), .en(ld_j), .clk(clk), .Q(j), .clr(reset));
  Subtractor #(.width(5)) subtractor_1 (
    .a(multiplexer_3_out), .b(5'b00001), .out(subtractor_1_out), .bin(1'b0));  // open: bout
  Adder #(.width(5)) adder_2 (
    .a(j), .b({5{1'b0}}), .out({adder_2_out[4], write_addr}), .cin(sl_j_plus_1_to_write_addr));  // open: cout
  Register #(.width(32)) elem2compare (
    .D(q_read_return_data), .en(ld_elem2compare), .clk(clk), .Q(elem2compare_q), .clr(reset));
  Register #(.width(32)) read_return_data (
    .D(r_data), .en(ld_return_read_data), .clk(clk), .Q(q_read_return_data), .clr(reset));
  Comparator #(.width(32)) comparator_1 (
    .a(elem2ins), .b(elem2compare_q), .gt(elem2insert_gt_elem2compare));  // open: eq, lt
  Multiplexer #(.width(32)) multiplexer_4 (
    .in0(elem2ins), .in1(elem2compare_q), .out(write_data), .sel(sl_elem2compare_to_write_data));
  Comparator #(.mode("unsigned"), .width(5)) comparator_2 (.a(j), .b({5{1'b0}}), .lt(comparator_2_lt));  // open: gt, eq
  not not_2 (j_gte_0, comparator_2_lt);
  Comparator #(.mode("unsigned"), .width(5)) comparator_3 (.a(i), .b(arr_size), .lt(i_lt_arr_size));  // open: gt, eq

  // Other names for the same wires on the sheet: d_read_return_data[31:0] = r_data
endmodule

module main (
  input  start,
  input  [4:0] in_2,
  input  rst_n,
  input  in_4,
  input  in_5,
  output out_6,
  output out_7
);

  wire clock_1_out, memory_1_ar_ready, memory_1_aw_ready, memory_1_b_resp, memory_1_b_valid, memory_1_r_resp,
       memory_1_r_valid, memory_1_w_ready, sort_circuit_1_ar_valid, sort_circuit_1_aw_valid,
       sort_circuit_1_b_ready, sort_circuit_1_r_ready, sort_circuit_1_w_valid;
  wire [3:0] sort_circuit_1_ar_address, sort_circuit_1_aw_address;
  wire [31:0] memory_1_r_data, sort_circuit_1_w_data;

  Clock clock_1 (.out(clock_1_out));
  sort_circuit sort_circuit_1 (
    .start(start), .arr_size(in_2), .ar_ready(memory_1_ar_ready), .r_valid(memory_1_r_valid),
    .r_resp(memory_1_r_resp), .r_data(memory_1_r_data), .aw_ready(memory_1_aw_ready),
    .w_ready(memory_1_w_ready), .b_valid(memory_1_b_valid), .b_resp(memory_1_b_resp), .clk(clock_1_out),
    .rst_n(rst_n), .done(out_6), .err(out_7), .ar_address(sort_circuit_1_ar_address),
    .ar_valid(sort_circuit_1_ar_valid), .r_ready(sort_circuit_1_r_ready), .aw_valid(sort_circuit_1_aw_valid),
    .aw_address(sort_circuit_1_aw_address), .w_data(sort_circuit_1_w_data), .w_valid(sort_circuit_1_w_valid),
    .b_ready(sort_circuit_1_b_ready));
  memory memory_1 (
    .ar_valid(sort_circuit_1_ar_valid), .aw_valid(sort_circuit_1_aw_valid),
    .ar_address(sort_circuit_1_ar_address), .aw_address(sort_circuit_1_aw_address),
    .w_data(sort_circuit_1_w_data), .w_valid(sort_circuit_1_w_valid), .r_ready(sort_circuit_1_r_ready),
    .b_ready(sort_circuit_1_b_ready), .clk(clock_1_out), .rst_n(rst_n), .always_success(in_4),
    .always_error(in_5), .aw_ready(memory_1_aw_ready), .ar_ready(memory_1_ar_ready),
    .r_data(memory_1_r_data), .w_ready(memory_1_w_ready), .r_valid(memory_1_r_valid),
    .r_resp(memory_1_r_resp), .b_valid(memory_1_b_valid), .b_resp(memory_1_b_resp));

  // Notes on the sheet:
  //   in_2: initial=0x10
endmodule
