// Logisim project test.circ as structural Verilog: 6 circuits, main circuit main
module main (
);

  controller controller_1 ();  // open: start, ar_ready, r_valid, r_resp, aw_ready, w_ready, b_valid, b_resp, elem2insert_gt_elem2compare, j_gte_0, i_lt_arr_size, clk, rst_n, done, sl_1_incd_to_i, ld_return_read_data, error, ld_i, sl_j_j_plus_1_to_arg_write_addr, ar_valid, sl_elem2insert_elem2compare_to_arg_write_data, sl_i_minus_1_decrd_to_j, ld_arg_write_addr, r_ready, ld_arg_write_data, ld_j, aw_valid, ld_elem2insert, ld_elem2compare, w_valid, sl_i_j_to_arg_read_addr, ld_arg_read_addr, b_ready
  memory_filler memory_filler_1 ();  // open: clk, rst_n, arr_size, aw_ready, w_ready, b_valid, b_resp, done, aw_valid, aw_address, w_data, w_valid, b_ready
  datapath datapath_1 ();  // open: arr_size, ld_elem2compare, ld_j, sl_i_minus_1_decrd_to_j, ld_i, sl_1_incd_to_i, ld_elem2insert, ld_arg_write_data, sl_elem2insert_elem2compare_to_arg_write_data, ld_arg_read_addr, sl_i_j_to_arg_read_addr, ld_arg_write_addr, sl_j_j_plus_1_to_arg_write_addr, r_data, ld_return_read_data, clk, rst_n, elem2insert_gt_elem2compare, j_gte_0, i_lt_arr_size, w_data, ar_address, aw_address
  memory_module memory_module_1 ();  // open: ar_valid, aw_valid, ar_address, aw_address, w_data, w_valid, r_ready, b_ready, clk, rst_n, aw_ready, ar_ready, r_data, w_ready, r_valid, r_resp, b_valid, b_resp
endmodule

module controller (
  input  start,
  input  ar_ready,
  input  r_valid,
  input  r_resp,
  input  aw_ready,
  input  w_ready,
  input  b_valid,
  input  b_resp,
  input  elem2insert_gt_elem2compare,
  input  j_gte_0,
  input  i_lt_arr_size,
  input  clk,
  input  rst_n,
  output done,
  output sl_1_incd_to_i,
  output ld_return_read_data,
  output error,
  output ld_i,
  output sl_j_j_plus_1_to_arg_write_addr,
  output ar_valid,
  output sl_elem2insert_elem2compare_to_arg_write_data,
  output sl_i_minus_1_decrd_to_j,
  output ld_arg_write_addr,
  output r_ready,
  output ld_arg_write_data,
  output ld_j,
  output aw_valid,
  output ld_elem2insert,
  output ld_elem2compare,
  output w_valid,
  output sl_i_j_to_arg_read_addr,
  output ld_arg_read_addr,
  output b_ready
);

  wire and_1_out, and_2_out, and_3_out, and_8_out, and_9_out, and_10_out, and_11_out, and_16_out, and_17_out,
       and_18_out, and_19_out, and_20_out, and_21_out, and_22_out, assign_i, assng_j, check_if_correct_place,
       complete_ar, complete_aw, complete_aw_and_w, complete_aw_wait_w_ready, complete_w,
       complete_w_wait_aw_ready, gen_assign_i, gen_complete_ar, gen_complete_aw, gen_complete_aw_and_w,
       gen_complete_aw_wait_w_ready, gen_complete_w, gen_complete_w_wait_aw_ready, gen_done, gen_err,
       gen_inc_i, gen_outer_loop_check, gen_process_b_resp, gen_process_r_data_resp, gen_read_arr_i,
       gen_read_arr_j, gen_read_function, gen_return_read_fn, gen_return_write_fn,
       gen_shift_elem2insert_left, ld_arg_return_state, reset, sl_to_state;
  wire [1:0] sl_to_arg_return_state;
  wire [5:0] arg_return_state_q, d_arg_return_state;
  wire [29:0] gen_state;
  wire [31:0] current_state, decoder_1_out0;
  wire [32:0] next_state;

  not not_1 (reset, rst_n);
  and and_1 (and_1_out, current_state[2], ~i_lt_arr_size);  // AND_Gate
  and and_2 (and_2_out, current_state[7], ~j_gte_0);  // AND_Gate
  and and_3 (and_3_out, check_if_correct_place, elem2insert_gt_elem2compare);
  or or_1 (ar_valid, current_state[15], current_state[16]);
  or or_2 (r_ready, complete_ar, current_state[18]);
  or or_3 (aw_valid, current_state[22], current_state[23], complete_w_wait_aw_ready);
  or or_4 (w_valid, current_state[22], current_state[23], complete_aw_wait_w_ready);
  or or_5 (b_ready, complete_aw, complete_w, complete_aw_and_w, current_state[29]);
  and and_4 (gen_state[0], current_state[0], ~start);  // AND_Gate
  and and_5 (gen_assign_i, current_state[0], start);
  or or_6 (gen_outer_loop_check, assign_i, sl_1_incd_to_i);
  or or_7 (gen_done, and_1_out, done);
  and and_6 (gen_read_arr_i, current_state[2], i_lt_arr_size);
  or or_8 (gen_inc_i, and_2_out, and_3_out, sl_i_minus_1_decrd_to_j);
  and and_7 (gen_read_arr_j, current_state[7], j_gte_0);
  Register #(.width(6)) arg_return_state (
    .D(d_arg_return_state), .en(ld_arg_return_state), .clk(clk), .Q(arg_return_state_q), .clr(reset));
  or or_9 (ld_i, sl_1_incd_to_i, assign_i);
  or or_10 (ld_j, sl_i_minus_1_decrd_to_j, assng_j);
  or or_11 (ld_arg_read_addr, current_state[4], sl_i_j_to_arg_read_addr);
  Decoder #(.enable("false"), .select(5)) decoder_1 (
    .out0(decoder_1_out0[0]), .out1(decoder_1_out0[1]), .out2(decoder_1_out0[2]), .out3(decoder_1_out0[3]),
    .out4(decoder_1_out0[4]), .out5(decoder_1_out0[5]), .out6(decoder_1_out0[6]), .out7(decoder_1_out0[7]),
    .out8(decoder_1_out0[8]), .out9(decoder_1_out0[9]), .out10(decoder_1_out0[10]),
    .out11(decoder_1_out0[11]), .out12(decoder_1_out0[12]), .out13(decoder_1_out0[13]),
    .out14(decoder_1_out0[14]), .out15(decoder_1_out0[15]), .out16(decoder_1_out0[16]),
    .out17(decoder_1_out0[17]), .out18(decoder_1_out0[18]), .out19(decoder_1_out0[19]),
    .out20(decoder_1_out0[20]), .out21(decoder_1_out0[21]), .out22(decoder_1_out0[22]),
    .out23(decoder_1_out0[23]), .out24(decoder_1_out0[24]), .out25(decoder_1_out0[25]),
    .out26(decoder_1_out0[26]), .out27(decoder_1_out0[27]), .out28(decoder_1_out0[28]),
    .out29(decoder_1_out0[29]), .out30(decoder_1_out0[30]), .out31(decoder_1_out0[31]),
    .sel(arg_return_state_q[4:0]));
  Multiplexer #(.width(33)) multiplexer_1 (
    .in0({gen_err, gen_return_write_fn, gen_process_b_resp, gen_state[29], gen_complete_aw_and_w, gen_complete_w, gen_complete_aw_wait_w_ready, gen_complete_aw, gen_complete_w_wait_aw_ready, gen_state[23], current_state[21], gen_state[21], gen_return_read_fn, gen_process_r_data_resp, gen_state[18], gen_complete_ar, gen_state[16], gen_read_function, 2'b00, gen_shift_elem2insert_left, ld_elem2compare, 1'b0, gen_read_arr_j, gen_inc_i, assng_j, ld_elem2insert, 1'b0, gen_read_arr_i, gen_done, gen_outer_loop_check, gen_assign_i, gen_state[0]}),
    .in1({arg_return_state_q[5], decoder_1_out0}), .out(next_state), .sel(sl_to_state));
  and and_8 (and_8_out, current_state[16], ~ar_ready);  // AND_Gate
  and and_9 (and_9_out, current_state[18], ~r_valid);  // AND_Gate
  and and_10 (and_10_out, current_state[23], ~aw_ready, ~w_ready);  // AND_Gate
  and and_11 (and_11_out, 1'b1, clk);
  Register #(.width(32)) register_1 (
    .D(next_state[32:1]), .en(1'b1), .clk(clk),
    .Q({error, current_state[31:29], complete_aw_and_w, complete_w, complete_aw_wait_w_ready, complete_aw, complete_w_wait_aw_ready, current_state[23:20], ld_return_read_data, current_state[18], complete_ar, current_state[16:15], sl_i_minus_1_decrd_to_j, sl_elem2insert_elem2compare_to_arg_write_data, current_state[12], check_if_correct_place, ld_elem2compare, sl_i_j_to_arg_read_addr, sl_1_incd_to_i, current_state[7], assng_j, ld_elem2insert, current_state[4], done, current_state[2], assign_i}),
    .clr(reset));
  and and_12 (gen_shift_elem2insert_left, check_if_correct_place, ~elem2insert_gt_elem2compare);  // AND_Gate
  or or_12 (gen_read_function, current_state[4], sl_i_j_to_arg_read_addr);
  or or_13 (gen_state[16], current_state[15], and_8_out);
  and and_13 (gen_complete_ar, current_state[16], ar_ready);
  or or_14 (gen_state[18], complete_ar, and_9_out);
  and and_14 (gen_process_r_data_resp, current_state[18], r_valid);
  and and_15 (gen_return_read_fn, ld_return_read_data, r_resp);
  or or_15 (gen_state[21], current_state[12], sl_elem2insert_elem2compare_to_arg_write_data);
  or or_16 (gen_state[23], current_state[22], and_10_out);
  D_Flip_Flop d_ff_1 (
    .D(next_state[0]), .clk(and_11_out), .Q(current_state[0]), .preset(reset), .reset(1'b0));  // open: Qn
  or or_17 (ld_arg_write_addr, sl_elem2insert_elem2compare_to_arg_write_data, current_state[12]);
  or or_18 (ld_arg_return_state, current_state[4], sl_i_j_to_arg_read_addr, current_state[12], sl_elem2insert_elem2compare_to_arg_write_data);
  or or_19 (sl_to_state, current_state[20], current_state[31]);
  Priority_Encoder #(.select(2)) priority_encoder_1 (
    .in0(current_state[4]), .in1(sl_i_j_to_arg_read_addr), .in2(current_state[12]),
    .in3(sl_elem2insert_elem2compare_to_arg_write_data), .out(sl_to_arg_return_state),
    .en_in(ld_arg_return_state));  // open: gs, en_out
  Multiplexer #(.select(2), .width(6)) multiplexer_2 (
    .in0(6'b000101), .in1(6'b001010), .in2(6'b001101), .in3(6'b001110), .out(d_arg_return_state),
    .sel(sl_to_arg_return_state));
  and and_16 (and_16_out, current_state[29], ~b_valid);  // AND_Gate
  and and_17 (and_17_out, current_state[23], w_ready, ~aw_ready);  // AND_Gate
  and and_18 (and_18_out, complete_w_wait_aw_ready, ~aw_ready);  // AND_Gate
  and and_19 (and_19_out, complete_aw_wait_w_ready, ~w_ready);  // AND_Gate
  and and_20 (and_20_out, ld_return_read_data, ~r_resp);  // AND_Gate
  and and_21 (and_21_out, current_state[30], ~b_resp);  // AND_Gate
  or or_20 (gen_complete_w_wait_aw_ready, and_17_out, and_18_out);
  or or_21 (gen_complete_aw_wait_w_ready, and_19_out, and_22_out);
  and and_22 (and_22_out, current_state[23], ~w_ready, aw_ready);  // AND_Gate
  and and_23 (gen_complete_aw, complete_w_wait_aw_ready, aw_ready);
  and and_24 (gen_complete_w, complete_aw_wait_w_ready, w_ready);
  and and_25 (gen_complete_aw_and_w, current_state[23], w_ready, aw_ready);
  and and_26 (gen_process_b_resp, current_state[29], b_valid);
  and and_27 (gen_return_write_fn, current_state[30], b_resp);
  or or_22 (gen_err, and_20_out, and_21_out);
  or or_23 (gen_state[29], complete_aw_and_w, complete_w, complete_aw, and_16_out);

  assign ld_arg_write_data = ld_arg_write_addr;
  assign sl_j_j_plus_1_to_arg_write_addr = sl_elem2insert_elem2compare_to_arg_write_data;

  // Other names for the same wires on the sheet: wait_start = current_state[0];
  //   current_state (some bits) = {error, complete_aw_and_w, complete_w, complete_aw_wait_w_ready, complete_aw, complete_w_wait_aw_ready, ld_return_read_data, complete_ar, sl_i_minus_1_decrd_to_j, sl_elem2insert_elem2compare_to_arg_write_data, check_if_correct_place, ld_elem2compare, sl_i_j_to_arg_read_addr, sl_1_incd_to_i, assng_j, ld_elem2insert, done, assign_i};
  //   outer_loop_check = current_state[2]; read_arr_i = current_state[4]; assign_elem2insert = ld_elem2insert;
  //   gen_assng_j = ld_elem2insert;
  //   gen_state (some bits) = {gen_err, gen_return_write_fn, gen_process_b_resp, gen_complete_aw_and_w, gen_complete_w, gen_complete_aw_wait_w_ready, gen_complete_aw, gen_complete_w_wait_aw_ready, current_state[21], gen_return_read_fn, gen_process_r_data_resp, gen_complete_ar, gen_read_function, gen_shift_elem2insert_left, ld_elem2compare, gen_read_arr_j, gen_inc_i, assng_j, ld_elem2insert, gen_read_arr_i, gen_done, gen_outer_loop_check, gen_assign_i};
  //   gen_inner_loop_check = assng_j; inner_loop_check = current_state[7]; inc_i = sl_1_incd_to_i;
  //   read_arr_j = sl_i_j_to_arg_read_addr; assign_elem2compare = ld_elem2compare;
  //   gen_check_if_correct_place = ld_elem2compare; shift_elem2insert_left = current_state[12];
  //   shif_elem2compare_right = sl_elem2insert_elem2compare_to_arg_write_data; decrmt_j_t = sl_i_minus_1_decrd_to_j;
  //   read_function = current_state[15]; wait_ar_ready = current_state[16]; wait_r_valid = current_state[18];
  //   process_r_data_resp = ld_return_read_data; return_read_fn = current_state[20];
  //   gen_send_addr_and_data = current_state[21]; write_function = current_state[21];
  //   send_addr_and_data = current_state[22]; wait_aw_ready_or_w_ready = current_state[23];
  //   wait_b_valid = current_state[29]; process_b_resp = current_state[30]; return_write_fn = current_state[31];
  //   err = error; e2ins_gt_e2cmp = elem2insert_gt_elem2compare; gen_wait_start = gen_state[0];
  //   gen_wait_ar_ready = gen_state[16]; gen_wait_r_valid = gen_state[18]; gen_write_function = gen_state[21];
  //   gen_wait_aw_ready_or_w_ready = gen_state[23]; gen_wait_b_valid = gen_state[29]

  // Notes on the sheet:
  //   Output Generation
  //   Next State Generation
  //   onehot encoding
  //   Internal Control Signal Generation
  //   those states reached via function return
endmodule

module datapath (
  input  [3:0] arr_size,
  input  ld_elem2compare,
  input  ld_j,
  input  sl_i_minus_1_decrd_to_j,
  input  ld_i,
  input  sl_1_incd_to_i,
  input  ld_elem2insert,
  input  ld_arg_write_data,
  input  sl_elem2insert_elem2compare_to_arg_write_data,
  input  ld_arg_read_addr,
  input  sl_i_j_to_arg_read_addr,
  input  ld_arg_write_addr,
  input  sl_j_j_plus_1_to_arg_write_addr,
  input  [31:0] r_data,
  input  ld_return_read_data,
  input  clk,
  input  rst_n,
  output elem2insert_gt_elem2compare,
  output j_gte_0,
  output i_lt_arr_size,
  output [31:0] w_data,
  output [3:0] ar_address,
  output [3:0] aw_address
);

  wire comparator_2_lt, not_1_out;
  wire [4:0] adder_1_out, adder_2_out, i_q, j_q, multiplexer_1_out, multiplexer_2_out, multiplexer_3_out,
       subtractor_1_out;
  wire [31:0] elem2compare_q, elem2insert_q, multiplexer_4_out, read_return_data_q;

  not not_1 (not_1_out, rst_n);
  Multiplexer #(.width(5)) multiplexer_1 (
    .in0(5'b00001), .in1(adder_1_out), .out(multiplexer_1_out), .sel(sl_1_incd_to_i));
  Adder #(.width(5)) adder_1 (.a(5'b00001), .b(i_q), .out(adder_1_out), .cin(1'b0));  // open: cout
  Register #(.width(5)) i (.D(multiplexer_1_out), .en(ld_i), .clk(clk), .Q(i_q), .clr(not_1_out));
  Register #(.width(4)) arg_read_addr (
    .D(multiplexer_3_out[3:0]), .en(ld_arg_read_addr), .clk(clk), .Q(ar_address), .clr(not_1_out));
  Register #(.width(32)) elem2insert (
    .D(read_return_data_q), .en(ld_elem2insert), .clk(clk), .Q(elem2insert_q), .clr(not_1_out));
  Register #(.width(32)) arg_write_data (
    .D(multiplexer_4_out), .en(ld_arg_write_data), .clk(clk), .Q(w_data), .clr(not_1_out));
  Multiplexer #(.width(5)) multiplexer_2 (.in0(i_q), .in1(j_q), .out(multiplexer_2_out), .sel(sl_i_minus_1_decrd_to_j));
  Adder #(.width(5)) adder_2 (
    .a(j_q), .b({5{1'b0}}), .out(adder_2_out), .cin(sl_j_j_plus_1_to_arg_write_addr));  // open: cout
  Register #(.width(5)) j (.D(subtractor_1_out), .en(ld_j), .clk(clk), .Q(j_q), .clr(not_1_out));
  Subtractor #(.width(5)) subtractor_1 (
    .a(multiplexer_2_out), .b(5'b00001), .out(subtractor_1_out), .bin(1'b0));  // open: bout
  Register #(.width(4)) arg_write_addr (
    .D(adder_2_out[3:0]), .en(ld_arg_write_addr), .clk(clk), .Q(aw_address), .clr(not_1_out));
  Multiplexer #(.width(5)) multiplexer_3 (.in0(i_q), .in1(j_q), .out(multiplexer_3_out), .sel(sl_i_j_to_arg_read_addr));
  Register #(.width(32)) elem2compare (
    .D(read_return_data_q), .en(ld_elem2compare), .clk(clk), .Q(elem2compare_q), .clr(not_1_out));
  Register #(.width(32)) read_return_data (
    .D(r_data), .en(ld_return_read_data), .clk(clk), .Q(read_return_data_q), .clr(not_1_out));
  Comparator #(.width(32)) comparator_1 (
    .a(elem2insert_q), .b(elem2compare_q), .gt(elem2insert_gt_elem2compare));  // open: eq, lt
  Multiplexer #(.width(32)) multiplexer_4 (
    .in0(elem2insert_q), .in1(elem2compare_q), .out(multiplexer_4_out),
    .sel(sl_elem2insert_elem2compare_to_arg_write_data));
  Comparator #(.width(5)) comparator_2 (.a(j_q), .b({5{1'b0}}), .lt(comparator_2_lt));  // open: gt, eq
  not not_2 (j_gte_0, comparator_2_lt);
  Comparator #(.width(5)) comparator_3 (.a({1'b0, arr_size}), .b(i_q), .gt(i_lt_arr_size));  // open: eq, lt

  // Notes on the sheet:
  //   rst
endmodule

module memory_module (
  input  ar_valid,
  input  aw_valid,
  input  [3:0] ar_address,
  input  [3:0] aw_address,
  input  [31:0] w_data,
  input  w_valid,
  input  r_ready,
  input  b_ready,
  input  clk,
  input  rst_n,
  output aw_ready,
  output ar_ready,
  output [31:0] r_data,
  output w_ready,
  output r_valid,
  output r_resp,
  output b_valid,
  output b_resp
);

  wire and_1_out, and_3_out, and_4_out, and_5_out, and_6_out, and_7_out, and_8_out, and_11_out, and_12_out,
       complete_ar, complete_aw, complete_b, complete_r, complete_w, gen_ar_transfer, gen_aw_transfer,
       gen_complete_b, gen_complete_r, gen_decide_random, gen_idle, ld_data, ld_reg_addr, reset,
       sl_ram_w_to_data;
  wire [3:0] reg_addr, rnd;
  wire [14:6] gen_state;
  wire [15:0] curr_state;
  wire [31:0] multiplexer_1_out, ram_out;

  and and_1 (and_1_out, curr_state[0], ~ar_valid, ~aw_valid);  // AND_Gate
  or or_1 (gen_idle, and_1_out, complete_r, complete_b);
  and and_2 (gen_decide_random, curr_state[0], ar_valid, aw_valid);
  and and_3 (and_3_out, curr_state[0], ar_valid, ~aw_valid);  // AND_Gate
  or or_2 (gen_ar_transfer, and_3_out, and_4_out);
  and and_4 (and_4_out, curr_state[1], ~rnd[0]);  // AND_Gate
  and and_5 (and_5_out, curr_state[0], ~ar_valid, aw_valid);  // AND_Gate
  and and_6 (and_6_out, curr_state[1], rnd[0]);
  not not_1 (reset, rst_n);
  or or_3 (gen_aw_transfer, and_5_out, and_6_out);
  and and_7 (and_7_out, curr_state[6], ~r_ready);  // AND_Gate
  and and_8 (and_8_out, curr_state[10], ~w_valid);  // AND_Gate
  or or_4 (gen_state[6], and_7_out, curr_state[7]);
  and and_9 (gen_complete_r, curr_state[6], r_ready);
  or or_5 (gen_state[10], and_8_out, complete_aw);
  and and_10 (gen_state[11], curr_state[10], w_valid);
  D_Flip_Flop d_ff_1 (.D(gen_idle), .clk(and_11_out), .Q(curr_state[0]), .preset(reset), .reset(1'b0));  // open: Qn
  and and_11 (and_11_out, 1'b1, clk);
  Register #(.width(16)) register_1 (
    .D({gen_complete_b, curr_state[13], gen_state[14], complete_w, w_ready, gen_state[11:10], aw_ready, gen_complete_r, curr_state[5], gen_state[6], complete_ar, ar_ready, gen_aw_transfer, gen_ar_transfer, gen_decide_random}),
    .en(1'b1), .clk(clk),
    .Q({complete_b, curr_state[15:13], complete_w, w_ready, curr_state[10], complete_aw, complete_r, curr_state[7:5], complete_ar, aw_ready, ar_ready, curr_state[1]}),
    .clr(reset));
  Multiplexer #(.width(32)) multiplexer_1 (
    .in0(ram_out), .in1(w_data), .out(multiplexer_1_out), .sel(sl_ram_w_to_data));
  Register #(.width(4)) u_reg_addr (.D(ar_address), .en(ld_reg_addr), .clk(clk), .Q(reg_addr), .clr(reset));
  Random #(.width(4)) random_1 (.clr(reset), .next(1'b1), .clk(clk), .out(rnd));
  Register #(.width(32)) reg_data (.D(multiplexer_1_out), .en(ld_data), .clk(clk), .Q(r_data), .clr(reset));
  and and_12 (and_12_out, curr_state[14], ~b_ready);  // AND_Gate
  or or_6 (gen_state[14], curr_state[15], and_12_out);
  and and_13 (gen_complete_b, curr_state[14], b_ready);
  RAM #(.addrWidth(4), .dataWidth(32)) ram_1 (
    .addr(reg_addr), .we(curr_state[13]), .oe(curr_state[5]), .clk(clk), .din(r_data), .dout(ram_out));
  nand nand_1 (b_resp, rnd[0], rnd[1], rnd[2], rnd[3]);
  or or_7 (b_valid, curr_state[15], curr_state[14]);
  or or_8 (r_valid, curr_state[7], curr_state[6]);
  not not_2 (sl_ram_w_to_data, curr_state[5]);
  or or_9 (ld_data, curr_state[5], w_ready);
  or or_10 (ld_reg_addr, aw_ready, ar_ready);

  assign r_resp = b_resp;

  // Other names for the same wires on the sheet: idle = curr_state[0]; decide_random = curr_state[1];
  //   wait_r_ready = curr_state[6]; output_read_data = curr_state[7];
  //   curr_state (some bits) = {complete_b, complete_w, w_ready, complete_aw, complete_r, complete_ar, aw_ready, ar_ready};
  //   wait_w_valid = curr_state[10]; wait_b_ready = curr_state[14]; respond_b = curr_state[15];
  //   gen_state (some bits) = {gen_complete_b, curr_state[13], complete_w, w_ready, aw_ready, gen_complete_r, curr_state[5], complete_ar, ar_ready, gen_aw_transfer, gen_ar_transfer, gen_decide_random, gen_idle};
  //   ar_transfer = ar_ready; gen_complete_ar = ar_ready; gen_register_read_data = complete_ar;
  //   gen_wait_r_ready = gen_state[6]; gen_output_read_data = curr_state[5]; out_enable = curr_state[5];
  //   register_read_data = curr_state[5]; aw_transfer = aw_ready; gen_complete_aw = aw_ready;
  //   gen_wait_w_valid = gen_state[10]; gen_w_transfer = gen_state[11]; gen_complete_w = w_ready;
  //   w_transfer = w_ready; gen_store_reg_data = complete_w; gen_wait_b_ready = gen_state[14];
  //   gen_respond_b = curr_state[13]; in_enable = curr_state[13]; store_reg_data = curr_state[13];
  //   ram_in[31:0] = r_data; reg_data[31:0] = r_data

  // Notes on the sheet:
  //   AXI-Lite interface
  //   State Transition Logic
  //   Onehot Encoded State
  //   Other Components
  //   State Output Logic
endmodule

module memory_filler (
  input  clk,
  input  rst_n,
  input  [3:0] arr_size,
  input  aw_ready,
  input  w_ready,
  input  b_valid,
  input  b_resp,
  output done,
  output aw_valid,
  output [3:0] aw_address,
  output [31:0] w_data,
  output w_valid,
  output b_ready
);

  wire and_1_out, and_2_out, and_3_out, check_i, gen_incr_i, gen_sdone, i_lt_arr_size, reset, submodule_done;
  wire [2:1] gen_state;
  wire [3:0] current_state;
  wire [4:0] d_i, r_i_q;
  wire [31:0] rnd;

  not not_1 (reset, rst_n);
  D_Flip_Flop d_ff_1 (.D(1'b0), .clk(clk), .Q(current_state[0]), .preset(reset), .reset(1'b0));  // open: Qn
  Register #(.width(5)) register_1 (
    .D({gen_sdone, current_state[3], gen_incr_i, gen_state}), .en(1'b1), .clk(clk),
    .Q({done, check_i, current_state[3:1]}), .clr(reset));
  and and_1 (and_1_out, check_i, i_lt_arr_size);
  and and_2 (and_2_out, current_state[2], ~submodule_done);  // AND_Gate
  and and_3 (and_3_out, check_i, ~i_lt_arr_size);  // AND_Gate
  Register #(.width(5)) r_i (.D(d_i), .en(current_state[3]), .clk(clk), .Q(r_i_q), .clr(reset));
  or or_1 (gen_state[1], current_state[0], and_1_out);
  or or_2 (gen_state[2], current_state[1], and_2_out);
  and and_4 (gen_incr_i, current_state[2], submodule_done);
  or or_3 (gen_sdone, and_3_out, done);
  Adder #(.width(5)) adder_1 (.a(r_i_q), .b({5{1'b0}}), .out(d_i), .cin(1'b1));  // open: cout
  Random #(.width(32)) random_1 (.clr(reset), .next(current_state[1]), .clk(clk), .out(rnd));
  Comparator #(.width(5)) comparator_1 (.a(r_i_q), .b({1'b0, arr_size}), .lt(i_lt_arr_size));  // open: gt, eq
  write_submodule write_submodule_1 (
    .start(current_state[1]), .aw_ready(aw_ready), .data(rnd), .addr(d_i[3:0]), .w_ready(w_ready),
    .b_valid(b_valid), .b_resp(b_resp), .clk(clk), .rst_n(rst_n), .aw_valid(aw_valid),
    .aw_address(aw_address), .done(submodule_done), .w_data(w_data), .w_valid(w_valid), .b_ready(b_ready));  // open: resp

  // Other names for the same wires on the sheet: initial = current_state[0]; en_rnd = current_state[1];
  //   submodule_start = current_state[1]; write_random_number = current_state[1];
  //   wait_submodule_return = current_state[2]; gen_check_i = current_state[3];
  //   gen_state[5:3] = {gen_sdone, current_state[3], gen_incr_i}; incr_i = current_state[3]; ld_i = current_state[3];
  //   current_state[5:4] = {done, check_i}; sdone = done; gen_write_random_number = gen_state[1];
  //   gen_wait_submodule_return = gen_state[2]

  // Notes on the sheet:
  //   User Interface
  //   Memory Interface
  //   State Transition
  //   Onehot Encoded State
  //   Other Components
  //   Output /Internal Control Sginal Generation
endmodule

module write_submodule (
  input  start,
  input  aw_ready,
  input  [31:0] data,
  input  [3:0] addr,
  input  w_ready,
  input  b_valid,
  input  b_resp,
  input  clk,
  input  rst_n,
  output aw_valid,
  output [3:0] aw_address,
  output done,
  output [31:0] w_data,
  output resp,
  output w_valid,
  output b_ready
);

  wire and_1_out, and_2_out, and_3_out, and_4_out, and_5_out, and_6_out, and_8_out, and_12_out, complete_aw,
       complete_aw_and_w, complete_aw_wait_w_ready, complete_w, complete_w_wait_aw_ready, gen_complete_aw,
       gen_complete_aw_and_w, gen_complete_aw_wait_w_ready, gen_complete_w, gen_complete_w_wait_aw_ready,
       gen_idle, gen_process_b_resp, gen_send_addr_and_data, reset;
  wire [3:0] reg_addr;
  wire [4:1] gen_state;
  wire [6:1] curr_state;
  wire [31:0] reg_data;

  not not_1 (reset, rst_n);
  and and_1 (and_1_out, done, ~start);  // AND_Gate
  and and_2 (and_2_out, curr_state[1], ~aw_ready, ~w_ready);  // AND_Gate
  and and_3 (and_3_out, complete_w_wait_aw_ready, ~aw_ready);  // AND_Gate
  and and_4 (and_4_out, curr_state[1], ~aw_ready, w_ready);  // AND_Gate
  and and_5 (and_5_out, complete_aw_wait_w_ready, ~w_ready);  // AND_Gate
  and and_6 (and_6_out, curr_state[1], aw_ready, ~w_ready);  // AND_Gate
  or or_1 (gen_idle, and_1_out, curr_state[6]);
  and and_7 (gen_send_addr_and_data, done, start);
  or or_2 (gen_state[1], curr_state[3], and_2_out);
  or or_3 (gen_complete_w_wait_aw_ready, and_3_out, and_4_out);
  or or_4 (gen_complete_aw_wait_w_ready, and_5_out, and_6_out);
  Register #(.width(32)) u_reg_data (.D(data), .en(done), .clk(clk), .Q(reg_data), .clr(reset));
  Register #(.width(1)) reg_b_resp (.D(b_resp), .en(1'b1), .clk(clk), .Q(resp), .clr(reset));
  D_Flip_Flop d_ff_1 (.D(gen_idle), .clk(and_8_out), .Q(done), .preset(reset), .reset(1'b0));  // open: Qn
  and and_8 (and_8_out, 1'b1, clk);
  Register #(.width(9)) register_1 (
    .D({gen_complete_aw_wait_w_ready, gen_complete_aw_and_w, gen_complete_w, gen_process_b_resp, gen_complete_aw, gen_state[4], gen_send_addr_and_data, gen_complete_w_wait_aw_ready, gen_state[1]}),
    .en(1'b1), .clk(clk),
    .Q({complete_aw_wait_w_ready, complete_aw_and_w, complete_w, curr_state[6], complete_aw, curr_state[4:3], complete_w_wait_aw_ready, curr_state[1]}),
    .clr(reset));
  Register #(.width(4)) u_reg_addr (.D(addr), .en(done), .clk(clk), .Q(reg_addr), .clr(reset));
  and and_9 (gen_complete_w, complete_aw_wait_w_ready, w_ready);
  and and_10 (gen_complete_aw, complete_w_wait_aw_ready, aw_ready);
  and and_11 (gen_complete_aw_and_w, curr_state[1], aw_ready, w_ready);
  and and_12 (and_12_out, curr_state[4], ~b_valid);  // AND_Gate
  or or_5 (gen_state[4], and_12_out, complete_w, complete_aw, complete_aw_and_w);
  and and_13 (gen_process_b_resp, curr_state[4], b_valid);
  or or_6 (aw_valid, curr_state[3], curr_state[1], complete_w_wait_aw_ready);
  or or_7 (w_valid, curr_state[3], curr_state[1], complete_aw_wait_w_ready);
  or or_8 (b_ready, complete_aw, complete_w, complete_aw_and_w);

  // Other names for the same wires on the sheet: curr_state (some bits) = {complete_aw_wait_w_ready, complete_aw_and_w, complete_w, complete_aw, complete_w_wait_aw_ready, done};
  //   idle = done; ld_reg_addr = done; ld_reg_data = done; wait_aw_ready_or_w_ready = curr_state[1];
  //   send_addr_and_data = curr_state[3]; wait_b_valid = curr_state[4]; process_b_resp = curr_state[6];
  //   gen_state (some bits) = {gen_complete_aw_wait_w_ready, gen_complete_aw_and_w, gen_complete_w, gen_process_b_resp, gen_complete_aw, gen_send_addr_and_data, gen_complete_w_wait_aw_ready, gen_idle};
  //   gen_wait_aw_ready_or_w_ready = gen_state[1]; gen_wait_b_valid = gen_state[4]; reg_b_resp = resp

  // Notes on the sheet:
  //   AXI-Lite interface
  //   Supermodule Interface
  //   State Generation
  //   Other Components
  //   Onehot Encoded State
  //   Output/Internal Control Signal Generation
endmodule
