// Logisim project test_module.circ as structural Verilog: 7 circuits, main circuit sort_circuit
module main (
  input  start,
  input  rst_n,
  input  sl_filler,
  output done,
  output err,
  output filler_done
);

  wire ar_ready, ar_valid, aw_ready, aw_ready_filler, aw_ready_sorter, aw_valid, aw_valid_filler,
       aw_valid_sorter, b_ready, b_ready_filler, b_ready_sorter, b_resp, b_resp_filler, b_resp_sorter,
       b_valid, b_valid_filler, b_valid_sorter, clk, r_ready, r_resp, r_valid, w_ready, w_ready_filler,
       w_ready_sorter, w_valid, w_valid_filler, w_valid_sorter;
  wire [3:0] ar_address, aw_address, aw_address_filler, aw_address_sorter;
  wire [31:0] r_data, w_data, w_data_filler, w_data_sorter;

  Clock clock_1 (.out(clk));
  sort_circuit sort_circuit_1 (
    .start(start), .r_valid(r_valid), .clk(clk), .r_resp(r_resp), .arr_size(5'b10000), .r_data(r_data),
    .ar_ready(ar_ready), .rst_n(rst_n), .aw_ready(aw_ready_sorter), .w_ready(w_ready_sorter),
    .b_valid(b_valid_sorter), .b_resp(b_resp_sorter), .done(done), .err(err), .ar_valid(ar_valid),
    .ar_address(ar_address), .r_ready(r_ready), .aw_valid(aw_valid_sorter), .w_valid(w_valid_sorter),
    .aw_address(aw_address_sorter), .w_data(w_data_sorter), .b_ready(b_ready_sorter));
  memory_filler memory_filler_1 (
    .clk(clk), .rst_n(rst_n), .arr_size(5'b10000), .aw_ready(aw_ready_filler), .w_ready(w_ready_filler),
    .b_valid(b_valid_filler), .b_resp(b_resp_filler), .done(filler_done), .aw_valid(aw_valid_filler),
    .aw_address(aw_address_filler), .w_data(w_data_filler), .w_valid(w_valid_filler), .b_ready(b_ready_filler));
  Multiplexer #(.width(39)) multiplexer_1 (
    .in0({b_ready_sorter, w_data_sorter, w_valid_sorter, aw_address_sorter, aw_valid_sorter}),
    .in1({b_ready_filler, w_data_filler, w_valid_filler, aw_address_filler, aw_valid_filler}),
    .out({b_ready, w_data, w_valid, aw_address, aw_valid}), .sel(sl_filler));
  Demultiplexer #(.width(4)) demultiplexer_1 (
    .out0({b_resp_sorter, b_valid_sorter, w_ready_sorter, aw_ready_sorter}),
    .out1({b_resp_filler, b_valid_filler, w_ready_filler, aw_ready_filler}),
    .in({b_resp, b_valid, w_ready, aw_ready}), .sel(sl_filler));
  memory_module memory_module_1 (
    .ar_valid(ar_valid), .aw_valid(aw_valid), .ar_address(ar_address), .aw_address(aw_address),
    .w_data(w_data), .w_valid(w_valid), .r_ready(r_ready), .b_ready(b_ready), .clk(clk), .rst_n(rst_n),
    .aw_ready(aw_ready), .ar_ready(ar_ready), .r_data(r_data), .w_ready(w_ready), .r_valid(r_valid),
    .r_resp(r_resp), .b_valid(b_valid), .b_resp(b_resp));
endmodule

module sort_circuit (
  input  start,
  input  r_valid,
  input  clk,
  input  r_resp,
  input  [4:0] arr_size,
  input  [31:0] r_data,
  input  ar_ready,
  input  rst_n,
  input  aw_ready,
  input  w_ready,
  input  b_valid,
  input  b_resp,
  output done,
  output err,
  output ar_valid,
  output [3:0] ar_address,
  output r_ready,
  output aw_valid,
  output w_valid,
  output [3:0] aw_address,
  output [31:0] w_data,
  output b_ready
);

  wire e2ins_gt_e2cmp, i_lt_arr_size, j_gte_0, ld_arg_read_addr, ld_e2cmp, ld_e2ins, ld_i, ld_j,
       ld_return_read_data, sl_decrd_to_j, sl_e2cmp_to_write_data, sl_incd_to_i, sl_j_p1_to_write_addr,
       sl_j_to_arg_read_addr, write_submodule_b_resp, write_submodule_done, write_submodule_start;
  wire [3:0] write_addr;
  wire [31:0] write_data;

  write_submodule write_submodule_1 (
    .start(write_submodule_start), .aw_ready(aw_ready), .data(write_data), .addr(write_addr),
    .w_ready(w_ready), .b_valid(b_valid), .b_resp(b_resp), .clk(clk), .rst_n(rst_n), .aw_valid(aw_valid),
    .aw_address(aw_address), .done(write_submodule_done), .w_data(w_data), .resp(write_submodule_b_resp),
    .w_valid(w_valid), .b_ready(b_ready));
  controller controller_1 (
    .start(start), .ar_ready(ar_ready), .r_valid(r_valid), .r_resp(r_resp),
    .write_submodule_done(write_submodule_done), .write_submodule_b_resp(write_submodule_b_resp),
    .elem2insert_gt_elem2compare(e2ins_gt_e2cmp), .j_gte_0(j_gte_0), .i_lt_arr_size(i_lt_arr_size),
    .clk(clk), .rst_n(rst_n), .done(done), .sl_incd_to_i(sl_incd_to_i),
    .ld_return_read_data(ld_return_read_data), .error(err), .ld_i(ld_i),
    .sl_j_plus_1_to_write_addr(sl_j_p1_to_write_addr),
    .sl_elem2compare_to_write_data(sl_e2cmp_to_write_data), .ar_valid(ar_valid),
    .sl_decrd_to_j(sl_decrd_to_j), .write_submodule_start(write_submodule_start), .r_ready(r_ready),
    .ld_j(ld_j), .ld_elem2insert(ld_e2ins), .ld_elem2compare(ld_e2cmp),
    .sl_j_to_arg_read_addr(sl_j_to_arg_read_addr), .ld_arg_read_addr(ld_arg_read_addr));
  datapath datapath_1 (
    .arr_size(arr_size), .ld_elem2insert(ld_e2ins), .ld_elem2compare(ld_e2cmp), .ld_j(ld_j),
    .sl_decrd_to_j(sl_decrd_to_j), .ld_i(ld_i), .sl_incd_to_i(sl_incd_to_i),
    .sl_elem2compare_to_write_data(sl_e2cmp_to_write_data), .sl_j_to_arg_read_addr(sl_j_to_arg_read_addr),
    .ld_arg_read_addr(ld_arg_read_addr), .sl_j_plus_1_to_write_addr(sl_j_p1_to_write_addr), .r_data(r_data),
    .ld_return_read_data(ld_return_read_data), .clk(clk), .rst_n(rst_n),
    .elem2insert_gt_elem2compare(e2ins_gt_e2cmp), .write_data(write_data), .j_gte_0(j_gte_0),
    .i_lt_arr_size(i_lt_arr_size), .ar_address(ar_address), .write_addr(write_addr));
endmodule

module write_submodule (
  input  start,
  input  aw_ready,
  input  [31:0] data,
  input  [3:0] addr,
  input  w_ready,
  input  b_valid,
  input  b_resp,
  input  clk,
  input  rst_n,
  output aw_valid,
  output [3:0] aw_address,
  output done,
  output [31:0] w_data,
  output resp,
  output w_valid,
  output b_ready
);

  wire and_1_out, and_2_out, and_3_out, and_4_out, and_5_out, and_6_out, and_8_out, and_12_out, complete_aw,
       complete_aw_and_w, complete_aw_wait_w_ready, complete_w, complete_w_wait_aw_ready, gen_complete_aw,
       gen_complete_aw_and_w, gen_complete_aw_wait_w_ready, gen_complete_w, gen_complete_w_wait_aw_ready,
       gen_idle, gen_process_b_resp, gen_send_addr_and_data, reset;
  wire [4:1] gen_state;
  wire [6:1] curr_state;

  and and_1 (and_1_out, done, ~start);  // AND_Gate
  not not_1 (reset, rst_n);
  and and_2 (and_2_out, curr_state[1], ~aw_ready, ~w_ready);  // AND_Gate
  and and_3 (and_3_out, complete_w_wait_aw_ready, ~aw_ready);  // AND_Gate
  and and_4 (and_4_out, curr_state[1], ~aw_ready, w_ready);  // AND_Gate
  and and_5 (and_5_out, complete_aw_wait_w_ready, ~w_ready);  // AND_Gate
  and and_6 (and_6_out, curr_state[1], aw_ready, ~w_ready);  // AND_Gate
  or or_1 (gen_idle, and_1_out, curr_state[6]);
  and and_7 (gen_send_addr_and_data, done, start);
  or or_2 (gen_state[1], curr_state[3], and_2_out);
  or or_3 (gen_complete_w_wait_aw_ready, and_3_out, and_4_out);
  or or_4 (gen_complete_aw_wait_w_ready, and_5_out, and_6_out);
  Register #(.width(32)) reg_data (.D(data), .en(done), .clk(clk), .Q(w_data), .clr(reset));
  Register #(.width(1)) reg_b_resp (.D(b_resp), .en(1'b1), .clk(clk), .Q(resp), .clr(reset));
  D_Flip_Flop d_ff_1 (.D(gen_idle), .clk(and_8_out), .Q(done), .preset(reset), .reset(1'b0));  // open: Qn
  and and_8 (and_8_out, 1'b1, clk);
  Register #(.width(9)) register_1 (
    .D({gen_complete_aw_wait_w_ready, gen_complete_aw_and_w, gen_complete_w, gen_process_b_resp, gen_complete_aw, gen_state[4], gen_send_addr_and_data, gen_complete_w_wait_aw_ready, gen_state[1]}),
    .en(1'b1), .clk(clk),
    .Q({complete_aw_wait_w_ready, complete_aw_and_w, complete_w, curr_state[6], complete_aw, curr_state[4:3], complete_w_wait_aw_ready, curr_state[1]}),
    .clr(reset));
  Register #(.width(4)) reg_addr (.D(addr), .en(done), .clk(clk), .Q(aw_address), .clr(reset));
  and and_9 (gen_complete_w, complete_aw_wait_w_ready, w_ready);
  and and_10 (gen_complete_aw, complete_w_wait_aw_ready, aw_ready);
  and and_11 (gen_complete_aw_and_w, curr_state[1], aw_ready, w_ready);
  and and_12 (and_12_out, curr_state[4], ~b_valid);  // AND_Gate
  or or_5 (gen_state[4], and_12_out, complete_w, complete_aw, complete_aw_and_w);
  and and_13 (gen_process_b_resp, curr_state[4], b_valid);
  or or_6 (aw_valid, curr_state[3], curr_state[1], complete_w_wait_aw_ready);
  or or_7 (w_valid, curr_state[3], curr_state[1], complete_aw_wait_w_ready);
  or or_8 (b_ready, complete_aw, complete_w, curr_state[4], complete_aw_and_w);

  // Other names for the same wires on the sheet: curr_state (some bits) = {complete_aw_wait_w_ready, complete_aw_and_w, complete_w, complete_aw, complete_w_wait_aw_ready, done};
  //   idle = done; ld_reg_addr = done; ld_reg_data = done; wait_aw_ready_or_w_ready = curr_state[1];
  //   send_addr_and_data = curr_state[3]; wait_b_valid = curr_state[4]; process_b_resp = curr_state[6];
  //   gen_state (some bits) = {gen_complete_aw_wait_w_ready, gen_complete_aw_and_w, gen_complete_w, gen_process_b_resp, gen_complete_aw, gen_send_addr_and_data, gen_complete_w_wait_aw_ready, gen_idle};
  //   gen_wait_aw_ready_or_w_ready = gen_state[1]; gen_wait_b_valid = gen_state[4]; reg_addr[3:0] = aw_address;
  //   reg_b_resp = resp; reg_data[31:0] = w_data

  // Notes on the sheet:
  //   AXI-Lite interface
  //   Supermodule Interface
  //   State Generation
  //   Other Components
  //   Onehot Encoded State
  //   Output/Internal Control Signal Generation
endmodule

module controller (
  input  start,
  input  ar_ready,
  input  r_valid,
  input  r_resp,
  input  write_submodule_done,
  input  write_submodule_b_resp,
  input  elem2insert_gt_elem2compare,
  input  j_gte_0,
  input  i_lt_arr_size,
  input  clk,
  input  rst_n,
  output done,
  output sl_incd_to_i,
  output ld_return_read_data,
  output error,
  output ld_i,
  output sl_j_plus_1_to_write_addr,
  output sl_elem2compare_to_write_data,
  output ar_valid,
  output sl_decrd_to_j,
  output write_submodule_start,
  output r_ready,
  output ld_j,
  output ld_elem2insert,
  output ld_elem2compare,
  output sl_j_to_arg_read_addr,
  output ld_arg_read_addr
);

  wire and_1_out, and_2_out, and_3_out, and_8_out, and_9_out, and_10_out, and_11_out, and_12_out, and_13_out,
       and_18_out, and_19_out, assign_i, assng_j, check_if_correct_place, complete_ar, gen_assign_i,
       gen_complete_ar, gen_decrmt_j, gen_done, gen_err, gen_inc_i, gen_outer_loop_check,
       gen_process_r_data_resp, gen_read_arr_i, gen_read_arr_j, gen_read_function, gen_return_read_fn,
       gen_shif_elem2compare_right, gen_shift_elem2insert_left, ld_arg_return_state, reset,
       sl_to_arg_return_state;
  wire [4:0] arg_return_state_q, d_arg_return_state;
  wire [20:0] gen_state;
  wire [22:0] current_state;
  wire [23:0] decoder_1_out0, next_state;

  not not_1 (reset, rst_n);
  and and_1 (and_1_out, current_state[2], ~i_lt_arr_size);  // AND_Gate
  and and_2 (and_2_out, current_state[7], ~j_gte_0);  // AND_Gate
  and and_3 (and_3_out, check_if_correct_place, elem2insert_gt_elem2compare);
  or or_1 (ar_valid, current_state[17], current_state[18]);
  or or_2 (r_ready, complete_ar, current_state[20]);
  and and_4 (gen_state[0], current_state[0], ~start);  // AND_Gate
  and and_5 (gen_assign_i, current_state[0], start);
  or or_3 (gen_outer_loop_check, assign_i, sl_incd_to_i);
  or or_4 (gen_done, and_1_out, done);
  and and_6 (gen_read_arr_i, current_state[2], i_lt_arr_size);
  or or_5 (gen_inc_i, and_2_out, and_3_out, sl_decrd_to_j);
  and and_7 (gen_read_arr_j, current_state[7], j_gte_0);
  Register #(.width(5)) arg_return_state (
    .D(d_arg_return_state), .en(ld_arg_return_state), .clk(clk), .Q(arg_return_state_q), .clr(reset));
  or or_6 (ld_i, sl_incd_to_i, assign_i);
  or or_7 (ld_j, sl_decrd_to_j, assng_j);
  or or_8 (ld_arg_read_addr, current_state[4], sl_j_to_arg_read_addr);
  Decoder #(.enable("false"), .select(5)) decoder_1 (
    .out0(decoder_1_out0[0]), .out1(decoder_1_out0[1]), .out2(decoder_1_out0[2]), .out3(decoder_1_out0[3]),
    .out4(decoder_1_out0[4]), .out5(decoder_1_out0[5]), .out6(decoder_1_out0[6]), .out7(decoder_1_out0[7]),
    .out8(decoder_1_out0[8]), .out9(decoder_1_out0[9]), .out10(decoder_1_out0[10]),
    .out11(decoder_1_out0[11]), .out12(decoder_1_out0[12]), .out13(decoder_1_out0[13]),
    .out14(decoder_1_out0[14]), .out15(decoder_1_out0[15]), .out16(decoder_1_out0[16]),
    .out17(decoder_1_out0[17]), .out18(decoder_1_out0[18]), .out19(decoder_1_out0[19]),
    .out20(decoder_1_out0[20]), .out21(decoder_1_out0[21]), .out22(decoder_1_out0[22]),
    .out23(decoder_1_out0[23]), .sel(arg_return_state_q));  // open: out24, out25, out26, out27, out28, out29, out30, out31
  Multiplexer #(.width(24)) multiplexer_1 (
    .in0({gen_err, gen_return_read_fn, gen_process_r_data_resp, gen_state[20], gen_complete_ar, gen_state[18], gen_read_function, gen_decrmt_j, gen_state[15], gen_shif_elem2compare_right, gen_state[13], gen_shift_elem2insert_left, ld_elem2compare, 1'b0, gen_read_arr_j, gen_inc_i, assng_j, ld_elem2insert, 1'b0, gen_read_arr_i, gen_done, gen_outer_loop_check, gen_assign_i, gen_state[0]}),
    .in1(decoder_1_out0), .out(next_state), .sel(current_state[22]));
  and and_8 (and_8_out, current_state[18], ~ar_ready);  // AND_Gate
  and and_9 (and_9_out, current_state[20], ~r_valid);  // AND_Gate
  and and_10 (and_10_out, ld_return_read_data, ~r_resp);  // AND_Gate
  and and_11 (and_11_out, gen_shif_elem2compare_right, ~write_submodule_b_resp);  // AND_Gate
  and and_12 (and_12_out, gen_decrmt_j, ~write_submodule_b_resp);  // AND_Gate
  and and_13 (and_13_out, 1'b1, clk);
  Register #(.width(23)) register_1 (
    .D(next_state[23:1]), .en(1'b1), .clk(clk),
    .Q({error, current_state[22], ld_return_read_data, current_state[20], complete_ar, current_state[18:17], sl_decrd_to_j, current_state[15], sl_elem2compare_to_write_data, current_state[13:12], check_if_correct_place, ld_elem2compare, sl_j_to_arg_read_addr, sl_incd_to_i, current_state[7], assng_j, ld_elem2insert, current_state[4], done, current_state[2], assign_i}),
    .clr(reset));
  and and_14 (gen_shift_elem2insert_left, check_if_correct_place, ~elem2insert_gt_elem2compare);  // AND_Gate
  or or_9 (gen_read_function, current_state[4], sl_j_to_arg_read_addr);
  or or_10 (gen_state[18], current_state[17], and_8_out);
  and and_15 (gen_complete_ar, current_state[18], ar_ready);
  or or_11 (gen_state[20], complete_ar, and_9_out);
  and and_16 (gen_process_r_data_resp, current_state[20], r_valid);
  and and_17 (gen_return_read_fn, ld_return_read_data, r_resp);
  or or_12 (gen_err, and_10_out, and_11_out, and_12_out);
  D_Flip_Flop d_ff_1 (
    .D(next_state[0]), .clk(and_13_out), .Q(current_state[0]), .preset(reset), .reset(1'b0));  // open: Qn
  or or_13 (write_submodule_start, current_state[12], sl_elem2compare_to_write_data);
  Multiplexer #(.width(5)) multiplexer_2 (
    .in0(5'b00101), .in1(5'b01010), .out(d_arg_return_state), .sel(sl_to_arg_return_state));
  and and_18 (and_18_out, current_state[13], ~write_submodule_done);  // AND_Gate
  or or_14 (gen_state[15], sl_elem2compare_to_write_data, and_19_out);
  and and_19 (and_19_out, current_state[15], ~write_submodule_done);  // AND_Gate
  and and_20 (gen_decrmt_j, current_state[15], write_submodule_done);
  or or_15 (gen_state[13], current_state[12], and_18_out);
  and and_21 (gen_shif_elem2compare_right, current_state[13], write_submodule_done);
  or or_16 (ld_arg_return_state, current_state[4], sl_j_to_arg_read_addr);
  Priority_Encoder #(.select(1)) priority_encoder_1 (
    .in0(current_state[4]), .in1(sl_j_to_arg_read_addr), .out(sl_to_arg_return_state),
    .en_in(ld_arg_return_state));  // open: gs, en_out

  assign sl_j_plus_1_to_write_addr = sl_elem2compare_to_write_data;

  // Other names for the same wires on the sheet: wait_start = current_state[0];
  //   current_state (some bits) = {error, ld_return_read_data, complete_ar, sl_decrd_to_j, sl_elem2compare_to_write_data, check_if_correct_place, ld_elem2compare, sl_j_to_arg_read_addr, sl_incd_to_i, assng_j, ld_elem2insert, done, assign_i};
  //   outer_loop_check = current_state[2]; read_arr_i = current_state[4]; assign_elem2insert = ld_elem2insert;
  //   gen_assng_j = ld_elem2insert;
  //   gen_state (some bits) = {gen_err, gen_return_read_fn, gen_process_r_data_resp, gen_complete_ar, gen_read_function, gen_decrmt_j, gen_shif_elem2compare_right, gen_shift_elem2insert_left, ld_elem2compare, gen_read_arr_j, gen_inc_i, assng_j, ld_elem2insert, gen_read_arr_i, gen_done, gen_outer_loop_check, gen_assign_i};
  //   gen_inner_loop_check = assng_j; inner_loop_check = current_state[7]; inc_i = sl_incd_to_i;
  //   read_arr_j = sl_j_to_arg_read_addr; assign_elem2compare = ld_elem2compare;
  //   gen_check_if_correct_place = ld_elem2compare; shift_elem2insert_left = current_state[12];
  //   wait_submodule_return1 = current_state[13]; shif_elem2compare_right = sl_elem2compare_to_write_data;
  //   wait_submodule_return2 = current_state[15]; decrmt_j = sl_decrd_to_j; read_function = current_state[17];
  //   wait_ar_ready = current_state[18]; wait_r_valid = current_state[20]; process_r_data_resp = ld_return_read_data;
  //   return_read_fn = current_state[22]; sl_to_state = current_state[22]; err = error;
  //   e2ins_gt_e2cmp = elem2insert_gt_elem2compare; gen_wait_start = gen_state[0];
  //   gen_wait_submodule_return1 = gen_state[13]; gen_wait_submodule_return2 = gen_state[15];
  //   gen_wait_ar_ready = gen_state[18]; gen_wait_r_valid = gen_state[20]

  // Notes on the sheet:
  //   Output Generation
  //   Next State Generation
  //   onehot encoding
  //   those states reached via function return
  //   Internal Control Signal Generation
endmodule

module datapath (
  input  [4:0] arr_size,
  input  ld_elem2insert,
  input  ld_elem2compare,
  input  ld_j,
  input  sl_decrd_to_j,
  input  ld_i,
  input  sl_incd_to_i,
  input  sl_elem2compare_to_write_data,
  input  sl_j_to_arg_read_addr,
  input  ld_arg_read_addr,
  input  sl_j_plus_1_to_write_addr,
  input  [31:0] r_data,
  input  ld_return_read_data,
  input  clk,
  input  rst_n,
  output elem2insert_gt_elem2compare,
  output [31:0] write_data,
  output j_gte_0,
  output i_lt_arr_size,
  output [3:0] ar_address,
  output [3:0] write_addr
);

  wire comparator_2_lt, reset;
  wire [4:0] adder_1_out, i, j, multiplexer_1_out, multiplexer_2_out, multiplexer_3_out, subtractor_1_out;
  wire [4:4] adder_2_out;
  wire [31:0] elem2compare_q, elem2ins, q_read_return_data;

  not not_1 (reset, rst_n);
  Multiplexer #(.width(5)) multiplexer_1 (
    .in0(5'b00001), .in1(adder_1_out), .out(multiplexer_1_out), .sel(sl_incd_to_i));
  Adder #(.width(5)) adder_1 (.a(5'b00001), .b(i), .out(adder_1_out), .cin(1'b0));  // open: cout
  Multiplexer #(.width(5)) multiplexer_2 (.in0(i), .in1(j), .out(multiplexer_2_out), .sel(sl_j_to_arg_read_addr));
  Register #(.width(5)) u_i (.D(multiplexer_1_out), .en(ld_i), .clk(clk), .Q(i), .clr(reset));
  Register #(.width(4)) arg_read_addr (
    .D(multiplexer_2_out[3:0]), .en(ld_arg_read_addr), .clk(clk), .Q(ar_address), .clr(reset));
  Register #(.width(32)) elem2insert (
    .D(q_read_return_data), .en(ld_elem2insert), .clk(clk), .Q(elem2ins), .clr(reset));
  Multiplexer #(.width(5)) multiplexer_3 (.in0(i), .in1(j), .out(multiplexer_3_out), .sel(sl_decrd_to_j));
  Register #(.width(5)) u_j (.D(subtractor_1_out), .en(ld_j), .clk(clk), .Q(j), .clr(reset));
  Subtractor #(.width(5)) subtractor_1 (
    .a(multiplexer_3_out), .b(5'b00001), .out(subtractor_1_out), .bin(1'b0));  // open: bout
  Adder #(.width(5)) adder_2 (
    .a(j), .b({5{1'b0}}), .out({adder_2_out[4], write_addr}), .cin(sl_j_plus_1_to_write_addr));  // open: cout
  Register #(.width(32)) elem2compare (
    .D(q_read_return_data), .en(ld_elem2compare), .clk(clk), .Q(elem2compare_q), .clr(reset));
  Register #(.width(32)) read_return_data (
    .D(r_data), .en(ld_return_read_data), .clk(clk), .Q(q_read_return_data), .clr(reset));
  Comparator #(.width(32)) comparator_1 (
    .a(elem2ins), .b(elem2compare_q), .gt(elem2insert_gt_elem2compare));  // open: eq, lt
  Multiplexer #(.width(32)) multiplexer_4 (
    .in0(elem2ins), .in1(elem2compare_q), .out(write_data), .sel(sl_elem2compare_to_write_data));
  Comparator #(.mode("unsigned"), .width(5)) comparator_2 (.a(j), .b({5{1'b0}}), .lt(comparator_2_lt));  // open: gt, eq
  not not_2 (j_gte_0, comparator_2_lt);
  Comparator #(.mode("unsigned"), .width(5)) comparator_3 (.a(arr_size), .b(i), .gt(i_lt_arr_size));  // open: eq, lt

  // Other names for the same wires on the sheet: d_read_return_data[31:0] = r_data
endmodule

module memory_filler (
  input  clk,
  input  rst_n,
  input  [4:0] arr_size,
  input  aw_ready,
  input  w_ready,
  input  b_valid,
  input  b_resp,
  output done,
  output aw_valid,
  output [3:0] aw_address,
  output [31:0] w_data,
  output w_valid,
  output b_ready
);

  wire and_1_out, and_2_out, and_3_out, check_i, gen_incr_i, gen_sdone, i_lt_arr_size, reset, submodule_done;
  wire [2:1] gen_state;
  wire [3:0] current_state;
  wire [4:0] d_i, i;
  wire [15:0] rnd;

  not not_1 (reset, rst_n);
  D_Flip_Flop d_ff_1 (.D(1'b0), .clk(clk), .Q(current_state[0]), .preset(reset), .reset(1'b0));  // open: Qn
  Register #(.width(5)) register_1 (
    .D({gen_sdone, current_state[3], gen_incr_i, gen_state}), .en(1'b1), .clk(clk),
    .Q({done, check_i, current_state[3:1]}), .clr(reset));
  and and_1 (and_1_out, check_i, i_lt_arr_size);
  and and_2 (and_2_out, current_state[2], ~submodule_done);  // AND_Gate
  and and_3 (and_3_out, check_i, ~i_lt_arr_size);  // AND_Gate
  Register #(.width(5)) r_i (.D(d_i), .en(current_state[3]), .clk(clk), .Q(i), .clr(reset));
  or or_1 (gen_state[1], current_state[0], and_1_out);
  or or_2 (gen_state[2], current_state[1], and_2_out);
  and and_4 (gen_incr_i, current_state[2], submodule_done);
  or or_3 (gen_sdone, and_3_out, done);
  Adder #(.width(5)) adder_1 (.a(i), .b({5{1'b0}}), .out(d_i), .cin(1'b1));  // open: cout
  Random #(.width(16)) random_1 (.clr(reset), .next(current_state[1]), .clk(clk), .out(rnd));
  Comparator #(.width(5)) comparator_1 (.a(i), .b(arr_size), .gt(i_lt_arr_size));  // open: eq, lt
  write_submodule write_submodule_1 (
    .start(current_state[1]), .aw_ready(aw_ready), .data({{16{1'b0}}, rnd}), .addr(i[3:0]),
    .w_ready(w_ready), .b_valid(b_valid), .b_resp(b_resp), .clk(clk), .rst_n(rst_n), .aw_valid(aw_valid),
    .aw_address(aw_address), .done(submodule_done), .w_data(w_data), .w_valid(w_valid), .b_ready(b_ready));  // open: resp

  // Other names for the same wires on the sheet: initial = current_state[0]; en_rnd = current_state[1];
  //   submodule_start = current_state[1]; write_random_number = current_state[1];
  //   wait_submodule_return = current_state[2]; gen_check_i = current_state[3];
  //   gen_state[5:3] = {gen_sdone, current_state[3], gen_incr_i}; incr_i = current_state[3]; ld_i = current_state[3];
  //   current_state[5:4] = {done, check_i}; sdone = done; gen_write_random_number = gen_state[1];
  //   gen_wait_submodule_return = gen_state[2]

  // Notes on the sheet:
  //   User Interface
  //   Memory Interface
  //   State Transition
  //   Onehot Encoded State
  //   Other Components
  //   Output /Internal Control Sginal Generation
endmodule

module memory_module (
  input  ar_valid,
  input  aw_valid,
  input  [3:0] ar_address,
  input  [3:0] aw_address,
  input  [31:0] w_data,
  input  w_valid,
  input  r_ready,
  input  b_ready,
  input  clk,
  input  rst_n,
  output aw_ready,
  output ar_ready,
  output [31:0] r_data,
  output w_ready,
  output r_valid,
  output r_resp,
  output b_valid,
  output b_resp
);

  wire and_1_out, and_3_out, and_4_out, and_5_out, and_6_out, and_7_out, and_8_out, and_9_out, and_10_out,
       and_11_out, and_13_out, and_14_out, and_15_out, and_16_out, and_17_out, complete_ar, complete_aw,
       complete_b, complete_r, complete_w, gen_ar_transfer, gen_aw_transfer, gen_complete_b, gen_complete_r,
       gen_decide_random, gen_idle, ld_data, ld_reg_addr, reset, sl_w_to_data;
  wire [3:0] multiplexer_1_out, reg_addr, rnd;
  wire [14:6] gen_state;
  wire [15:0] curr_state;
  wire [31:0] multiplexer_2_out, ram_out;

  and and_1 (and_1_out, curr_state[0], ~ar_valid, ~aw_valid);  // AND_Gate
  or or_1 (gen_idle, and_1_out, complete_r, complete_b);
  and and_2 (gen_decide_random, curr_state[0], ar_valid, aw_valid);
  and and_3 (and_3_out, curr_state[0], ar_valid, ~aw_valid);  // AND_Gate
  or or_2 (gen_ar_transfer, and_3_out, and_4_out);
  and and_4 (and_4_out, curr_state[1], ~rnd[0]);  // AND_Gate
  and and_5 (and_5_out, curr_state[0], ~ar_valid, aw_valid);  // AND_Gate
  and and_6 (and_6_out, curr_state[1], rnd[0]);
  not not_1 (reset, rst_n);
  or or_3 (gen_aw_transfer, and_5_out, and_6_out);
  and and_7 (and_7_out, curr_state[6], ~r_ready);  // AND_Gate
  and and_8 (and_8_out, curr_state[7], ~r_ready);  // AND_Gate
  and and_9 (and_9_out, curr_state[7], r_ready);
  and and_10 (and_10_out, curr_state[6], r_ready);
  and and_11 (and_11_out, curr_state[10], ~w_valid);  // AND_Gate
  Multiplexer #(.width(4)) multiplexer_1 (.in0(ar_address), .in1(aw_address), .out(multiplexer_1_out), .sel(aw_ready));
  or or_4 (gen_state[6], and_7_out, and_8_out);
  or or_5 (gen_complete_r, and_9_out, and_10_out);
  or or_6 (gen_state[10], and_11_out, complete_aw);
  and and_12 (gen_state[11], curr_state[10], w_valid);
  D_Flip_Flop d_ff_1 (.D(gen_idle), .clk(and_13_out), .Q(curr_state[0]), .preset(reset), .reset(1'b0));  // open: Qn
  and and_13 (and_13_out, 1'b1, clk);
  Register #(.width(16)) register_1 (
    .D({gen_complete_b, curr_state[13], gen_state[14], complete_w, w_ready, gen_state[11:10], aw_ready, gen_complete_r, curr_state[5], gen_state[6], complete_ar, ar_ready, gen_aw_transfer, gen_ar_transfer, gen_decide_random}),
    .en(1'b1), .clk(clk),
    .Q({complete_b, curr_state[15:13], complete_w, w_ready, curr_state[10], complete_aw, complete_r, curr_state[7:5], complete_ar, aw_ready, ar_ready, curr_state[1]}),
    .clr(reset));
  Multiplexer #(.width(32)) multiplexer_2 (.in0(ram_out), .in1(w_data), .out(multiplexer_2_out), .sel(sl_w_to_data));
  Register #(.width(4)) u_reg_addr (.D(multiplexer_1_out), .en(ld_reg_addr), .clk(clk), .Q(reg_addr), .clr(reset));
  Random #(.width(4)) random_1 (.clr(reset), .next(1'b1), .clk(clk), .out(rnd));
  Register #(.width(32)) reg_data (.D(multiplexer_2_out), .en(ld_data), .clk(clk), .Q(r_data), .clr(reset));
  and and_14 (and_14_out, curr_state[15], ~b_ready);  // AND_Gate
  and and_15 (and_15_out, curr_state[14], ~b_ready);  // AND_Gate
  and and_16 (and_16_out, curr_state[14], b_ready);
  and and_17 (and_17_out, curr_state[15], b_ready);
  or or_7 (gen_state[14], and_14_out, and_15_out);
  or or_8 (gen_complete_b, and_16_out, and_17_out);
  RAM #(.addrWidth(4), .dataWidth(32)) ram_1 (
    .addr(reg_addr), .we(curr_state[13]), .oe(curr_state[5]), .clk(clk), .din(r_data), .dout(ram_out));
  nand nand_1 (b_resp, rnd[0], rnd[1], rnd[2], rnd[3]);
  or or_9 (b_valid, curr_state[15], curr_state[14]);
  or or_10 (r_valid, curr_state[7], curr_state[6]);
  not not_2 (sl_w_to_data, curr_state[5]);
  or or_11 (ld_data, curr_state[5], w_ready);
  or or_12 (ld_reg_addr, aw_ready, ar_ready);

  assign r_resp = b_resp;

  // Other names for the same wires on the sheet: idle = curr_state[0]; decide_random = curr_state[1];
  //   wait_r_ready = curr_state[6]; output_read_data = curr_state[7];
  //   curr_state (some bits) = {complete_b, complete_w, w_ready, complete_aw, complete_r, complete_ar, aw_ready, ar_ready};
  //   wait_w_valid = curr_state[10]; wait_b_ready = curr_state[14]; respond_b = curr_state[15];
  //   gen_state (some bits) = {gen_complete_b, curr_state[13], complete_w, w_ready, aw_ready, gen_complete_r, curr_state[5], complete_ar, ar_ready, gen_aw_transfer, gen_ar_transfer, gen_decide_random, gen_idle};
  //   ar_transfer = ar_ready; gen_complete_ar = ar_ready; gen_register_read_data = complete_ar;
  //   gen_wait_r_ready = gen_state[6]; gen_output_read_data = curr_state[5]; out_enable = curr_state[5];
  //   register_read_data = curr_state[5]; aw_transfer = aw_ready; gen_complete_aw = aw_ready;
  //   sl_aw_to_addr = aw_ready; gen_wait_w_valid = gen_state[10]; gen_w_transfer = gen_state[11];
  //   gen_complete_w = w_ready; w_transfer = w_ready; gen_store_reg_data = complete_w;
  //   gen_wait_b_ready = gen_state[14]; gen_respond_b = curr_state[13]; in_enable = curr_state[13];
  //   store_reg_data = curr_state[13]; ram_in[31:0] = r_data; reg_data[31:0] = r_data

  // Notes on the sheet:
  //   AXI-Lite interface
  //   State Transition Logic
  //   Onehot Encoded State
  //   Other Components
  //   State Output Logic
endmodule
