// Logisim project write_submodule.circ as structural Verilog: 1 circuit, main circuit write_submodule
module write_submodule (
  input  start,
  input  aw_ready,
  input  [31:0] data,
  input  [3:0] addr,
  input  w_ready,
  input  b_valid,
  input  b_resp,
  input  clk,
  input  rst_n,
  output aw_valid,
  output [3:0] aw_address,
  output done,
  output [31:0] w_data,
  output resp,
  output w_valid,
  output b_ready
);

  wire and_1_out, and_2_out, and_3_out, and_4_out, and_5_out, and_6_out, and_8_out, and_12_out, complete_aw,
       complete_aw_and_w, complete_aw_wait_w_ready, complete_w, complete_w_wait_aw_ready, gen_complete_aw,
       gen_complete_aw_and_w, gen_complete_aw_wait_w_ready, gen_complete_w, gen_complete_w_wait_aw_ready,
       gen_idle, gen_process_b_resp, gen_send_addr_and_data, reset;
  wire [3:0] reg_addr;
  wire [4:1] gen_state;
  wire [6:1] curr_state;
  wire [31:0] reg_data;

  not not_1 (reset, rst_n);
  and and_1 (and_1_out, done, ~start);  // AND_Gate
  and and_2 (and_2_out, curr_state[1], ~aw_ready, ~w_ready);  // AND_Gate
  and and_3 (and_3_out, complete_w_wait_aw_ready, ~aw_ready);  // AND_Gate
  and and_4 (and_4_out, curr_state[1], ~aw_ready, w_ready);  // AND_Gate
  and and_5 (and_5_out, complete_aw_wait_w_ready, ~w_ready);  // AND_Gate
  and and_6 (and_6_out, curr_state[1], aw_ready, ~w_ready);  // AND_Gate
  or or_1 (gen_idle, and_1_out, curr_state[6]);
  and and_7 (gen_send_addr_and_data, done, start);
  or or_2 (gen_state[1], curr_state[3], and_2_out);
  or or_3 (gen_complete_w_wait_aw_ready, and_3_out, and_4_out);
  or or_4 (gen_complete_aw_wait_w_ready, and_5_out, and_6_out);
  Register #(.width(32)) u_reg_data (.D(data), .en(done), .clk(clk), .Q(reg_data), .clr(reset));
  Register #(.width(1)) reg_b_resp (.D(b_resp), .en(1'b1), .clk(clk), .Q(resp), .clr(reset));
  D_Flip_Flop d_ff_1 (.D(gen_idle), .clk(and_8_out), .Q(done), .preset(reset), .reset(1'b0));  // open: Qn
  and and_8 (and_8_out, 1'b1, clk);
  Register #(.width(9)) register_1 (
    .D({gen_complete_aw_wait_w_ready, gen_complete_aw_and_w, gen_complete_w, gen_process_b_resp, gen_complete_aw, gen_state[4], gen_send_addr_and_data, gen_complete_w_wait_aw_ready, gen_state[1]}),
    .en(1'b1), .clk(clk),
    .Q({complete_aw_wait_w_ready, complete_aw_and_w, complete_w, curr_state[6], complete_aw, curr_state[4:3], complete_w_wait_aw_ready, curr_state[1]}),
    .clr(reset));
  Register #(.width(4)) u_reg_addr (.D(addr), .en(done), .clk(clk), .Q(reg_addr), .clr(reset));
  and and_9 (gen_complete_w, complete_aw_wait_w_ready, w_ready);
  and and_10 (gen_complete_aw, complete_w_wait_aw_ready, aw_ready);
  and and_11 (gen_complete_aw_and_w, curr_state[1], aw_ready, w_ready);
  and and_12 (and_12_out, curr_state[4], ~b_valid);  // AND_Gate
  or or_5 (gen_state[4], and_12_out, complete_w, complete_aw, complete_aw_and_w);
  and and_13 (gen_process_b_resp, curr_state[4], b_valid);
  or or_6 (aw_valid, curr_state[3], curr_state[1], complete_w_wait_aw_ready);
  or or_7 (w_valid, curr_state[3], curr_state[1], complete_aw_wait_w_ready);
  or or_8 (b_ready, complete_aw, complete_w, complete_aw_and_w);

  // Other names for the same wires on the sheet: curr_state (some bits) = {complete_aw_wait_w_ready, complete_aw_and_w, complete_w, complete_aw, complete_w_wait_aw_ready, done};
  //   idle = done; ld_reg_addr = done; ld_reg_data = done; wait_aw_ready_or_w_ready = curr_state[1];
  //   send_addr_and_data = curr_state[3]; wait_b_valid = curr_state[4]; process_b_resp = curr_state[6];
  //   gen_state (some bits) = {gen_complete_aw_wait_w_ready, gen_complete_aw_and_w, gen_complete_w, gen_process_b_resp, gen_complete_aw, gen_send_addr_and_data, gen_complete_w_wait_aw_ready, gen_idle};
  //   gen_wait_aw_ready_or_w_ready = gen_state[1]; gen_wait_b_valid = gen_state[4]; reg_b_resp = resp

  // Notes on the sheet:
  //   AXI-Lite interface
  //   Supermodule Interface
  //   State Generation
  //   Other Components
  //   Onehot Encoded State
  //   Output/Internal Control Signal Generation
endmodule
